// Logisim project Sagui_Vetorial.circ as structural Verilog: 14 circuits, main circuit main
module main (
);

  wire Br, Clk, IsBr, MD, MD0, MD1, MD2, MD3, Nop, not_1_out, not_2_out, not_3_out, not_4_out, not_5_out,
       not_6_out, not_7_out, not_8_out, not_9_out, not_10_out, not_11_out, not_12_out, R, RAD, RAD0, RAD1,
       RAD2, RAD3, spe_ula_1_zero, USr0, USr1, USr2, USr3, W, WE, WE0, WE1, WE2, WE3, WM0, WM1, WM2, WM3;
  wire [1:0] ID, IdV0, IdV1, IdV2, IdV3, MEM, memory_instruction_1_inst, MemV0, MemV1, MemV2, MemV3,
       multiplexer_2_out, multiplexer_3_out, multiplexer_4_out, multiplexer_5_out, multiplexer_6_out, RB_ID,
       UOp0, UOp1, UOp2, UOp3, USr;
  wire [2:0] ExeV0, ExeV1, ExeV2, ExeV3, UOp;
  wire [3:0] Opcode;
  wire [5:0] EXE;
  wire [6:0] VS;
  wire [7:0] adder_1_out, d0, d1, d2, d3, Data, imm, multiplexer_1_out, multiplexer_12_out,
       multiplexer_13_out, multiplexer_14_out, multiplexer_15_out, multiplexer_16_out,
       program_counter_1_pc_n, RA, RA0, RA1, RA2, RA3, RB, RB0, RB1, RB2, RB3, spe_memory_data_1_data,
       spe_ula_1_out_4, vpe_memory_data_1_data, vpe_memory_data_2_data, vpe_memory_data_3_data,
       vpe_memory_data_4_data, vpe_ula_1_out_4, vpe_ula_2_out_4, vpe_ula_3_out_4, vpe_ula_4_out_4;

  Multiplexer #(.width(8)) multiplexer_1 (.in0(adder_1_out), .in1(RB), .out(multiplexer_1_out), .sel(IsBr));
  Clock clock_1 (.out(Clk));
  Button Reset (.out(R));
  Program_Counter program_counter_1 (.PC_P(multiplexer_1_out), .Clk(Clk), .R(R), .PC_N(program_counter_1_pc_n));
  Adder adder_1 (.a(program_counter_1_pc_n), .b(8'h1), .out(adder_1_out));  // open: cin, cout
  Memory_Instruction memory_instruction_1 (
    .Addr_PC(program_counter_1_pc_n), .Inst({Opcode, RB_ID, memory_instruction_1_inst}));
  VPE_Ctrl vpe_ctrl_1 (.VectorSigns(VS), .ID_V(IdV0), .EXE_V(ExeV0), .MEM_V(MemV0));
  VPE_Ctrl vpe_ctrl_2 (.VectorSigns(VS), .ID_V(IdV1), .EXE_V(ExeV1), .MEM_V(MemV1));
  VPE_Ctrl vpe_ctrl_3 (.VectorSigns(VS), .ID_V(IdV2), .EXE_V(ExeV2), .MEM_V(MemV2));
  VPE_Ctrl vpe_ctrl_4 (.VectorSigns(VS), .ID_V(IdV3), .EXE_V(ExeV3), .MEM_V(MemV3));
  Multiplexer #(.width(2)) multiplexer_2 (
    .in0(memory_instruction_1_inst), .in1(2'b01), .out(multiplexer_2_out), .sel(RAD));
  Multiplexer #(.width(2)) multiplexer_3 (.in0(RB_ID), .in1(2'b01), .out(multiplexer_3_out), .sel(RAD0));
  Multiplexer #(.width(2)) multiplexer_4 (.in0(RB_ID), .in1(2'b01), .out(multiplexer_4_out), .sel(RAD1));
  Multiplexer #(.width(2)) multiplexer_5 (.in0(RB_ID), .in1(2'b01), .out(multiplexer_5_out), .sel(RAD2));
  Multiplexer #(.width(2)) multiplexer_6 (.in0(RB_ID), .in1(2'b01), .out(multiplexer_6_out), .sel(RAD3));
  Multiplexer #(.width(2)) multiplexer_7 (.in0(ID), .in1(2'b00), .out({RAD, WE}), .sel(Nop));
  assign imm = {{4{RB_ID[1]}}, {RB_ID, memory_instruction_1_inst}};  // Bit_Extender bit_extender_1
  SPE_Register_Bank spe_register_bank_1 (
    .WE(WE), .Data(Data), .RD(multiplexer_2_out), .Clk(Clk), .R(R), .RA(multiplexer_2_out), .RB(RB_ID),
    .RD1(RA), .RD2(RB));
  Multiplexer #(.width(2)) multiplexer_8 (.in0(2'b00), .in1(IdV0), .out({WE0, RAD0}), .sel(not_1_out));
  not not_1 (not_1_out, Nop);
  VPE0_Register_Bank vpe0_register_bank_1 (
    .WE(WE0), .Data(d0), .RD(multiplexer_3_out), .Clk(Clk), .R(R), .RA(multiplexer_3_out), .RB(RB_ID),
    .RD1(RA0), .RD2(RB0));
  Multiplexer #(.width(2)) multiplexer_9 (.in0(2'b00), .in1(IdV1), .out({WE1, RAD1}), .sel(not_2_out));
  not not_2 (not_2_out, Nop);
  Multiplexer #(.width(2)) multiplexer_10 (.in0(2'b00), .in1(IdV2), .out({WE2, RAD2}), .sel(not_3_out));
  not not_3 (not_3_out, Nop);
  Multiplexer #(.width(2)) multiplexer_11 (.in0(2'b00), .in1(IdV3), .out({WE3, RAD3}), .sel(not_4_out));
  not not_4 (not_4_out, Nop);
  Control_Unit control_unit_1 (
    .Opcode(Opcode), .Vec(Nop), .WE(ID[0]), .RadSpe(ID[1]), .UlaOpSpe(EXE[2:0]), .UlaSrSpe(EXE[4:3]),
    .BrSpe(EXE[5]), .MD(MEM[0]), .WM(MEM[1]), .VecSg(VS));
  VPE1_Register_Bank vpe1_register_bank_1 (
    .WE(WE1), .Data(d1), .RD(multiplexer_4_out), .Clk(Clk), .R(R), .RA(multiplexer_4_out), .RB(RB_ID),
    .RD1(RA1), .RD2(RB1));
  VPE2_Register_Bank vpe2_register_bank_1 (
    .WE(WE2), .Data(d2), .RD(multiplexer_5_out), .Clk(Clk), .R(R), .RA(multiplexer_5_out), .RB(RB_ID),
    .RD1(RA2), .RD2(RB2));
  VPE3_Register_Bank vpe3_register_bank_1 (
    .WE(WE3), .Data(d3), .RD(multiplexer_6_out), .Clk(Clk), .R(R), .RA(multiplexer_6_out), .RB(RB_ID),
    .RD1(RA3), .RD2(RB3));
  Multiplexer #(.select(2), .width(8)) multiplexer_12 (
    .in0(RB), .in1(imm), .in2({8{1'b0}}), .in3({8{1'b0}}), .out(multiplexer_12_out), .sel(USr));
  Multiplexer #(.width(8)) multiplexer_13 (.in0(RB0), .in1(imm), .out(multiplexer_13_out), .sel(USr0));
  Multiplexer #(.width(8)) multiplexer_14 (.in0(RB1), .in1(imm), .out(multiplexer_14_out), .sel(USr1));
  Multiplexer #(.width(8)) multiplexer_15 (.in0(RB2), .in1(imm), .out(multiplexer_15_out), .sel(USr2));
  Multiplexer #(.width(8)) multiplexer_16 (.in0(RB3), .in1(imm), .out(multiplexer_16_out), .sel(USr3));
  Multiplexer #(.width(6)) multiplexer_17 (.in0(EXE), .in1({6{1'b0}}), .out({Br, USr, UOp}), .sel(Nop));
  Multiplexer #(.width(3)) multiplexer_18 (.in0(3'b000), .in1(ExeV0), .out({USr0, UOp0}), .sel(not_5_out));
  not not_5 (not_5_out, Nop);
  Multiplexer #(.width(3)) multiplexer_19 (.in0(3'b000), .in1(ExeV1), .out({USr1, UOp1}), .sel(not_6_out));
  not not_6 (not_6_out, Nop);
  Multiplexer #(.width(3)) multiplexer_20 (.in0(3'b000), .in1(ExeV2), .out({USr2, UOp2}), .sel(not_7_out));
  not not_7 (not_7_out, Nop);
  Multiplexer #(.width(3)) multiplexer_21 (.in0(3'b000), .in1(ExeV3), .out({USr3, UOp3}), .sel(not_8_out));
  not not_8 (not_8_out, Nop);
  SPE_ULA spe_ula_1 (.ULA_Op(UOp), .RA(RA), .RB(multiplexer_12_out), .out_4(spe_ula_1_out_4), .Zero(spe_ula_1_zero));
  VPE_ULA vpe_ula_1 (.ULA_Op(UOp0), .RA(RA0), .RB(multiplexer_13_out), .out_4(vpe_ula_1_out_4));
  VPE_ULA vpe_ula_2 (.ULA_Op(UOp1), .RA(RA1), .RB(multiplexer_14_out), .out_4(vpe_ula_2_out_4));
  VPE_ULA vpe_ula_3 (.ULA_Op(UOp2), .RA(RA2), .RB(multiplexer_15_out), .out_4(vpe_ula_3_out_4));
  VPE_ULA vpe_ula_4 (.ULA_Op(UOp3), .RA(RA3), .RB(multiplexer_16_out), .out_4(vpe_ula_4_out_4));
  and and_1 (IsBr, Br, spe_ula_1_zero);
  Multiplexer #(.width(2)) multiplexer_22 (.in0(2'b00), .in1(MemV0), .out({WM0, MD0}), .sel(not_9_out));
  not not_9 (not_9_out, Nop);
  Multiplexer #(.width(2)) multiplexer_23 (.in0(2'b00), .in1(MemV1), .out({WM1, MD1}), .sel(not_10_out));
  not not_10 (not_10_out, Nop);
  Multiplexer #(.width(2)) multiplexer_24 (.in0(2'b00), .in1(MemV2), .out({WM2, MD2}), .sel(not_11_out));
  not not_11 (not_11_out, Nop);
  Multiplexer #(.width(2)) multiplexer_25 (.in0(2'b00), .in1(MemV3), .out({WM3, MD3}), .sel(not_12_out));
  not not_12 (not_12_out, Nop);
  VPE_Memory_Data vpe_memory_data_1 (.Addr(RB0), .WM(WM0), .Clk(Clk), .d(RA0), .data(vpe_memory_data_1_data));
  VPE_Memory_Data vpe_memory_data_2 (.Addr(RB1), .WM(WM1), .Clk(Clk), .d(RA1), .data(vpe_memory_data_2_data));
  VPE_Memory_Data vpe_memory_data_3 (.Addr(RB2), .WM(WM2), .Clk(Clk), .d(RA2), .data(vpe_memory_data_3_data));
  VPE_Memory_Data vpe_memory_data_4 (.Addr(RB3), .WM(WM3), .Clk(Clk), .d(RA3), .data(vpe_memory_data_4_data));
  Multiplexer #(.width(2)) multiplexer_26 (.in0(MEM), .in1(2'b00), .out({W, MD}), .sel(Nop));
  Multiplexer #(.width(8)) multiplexer_27 (.in0(vpe_ula_1_out_4), .in1(vpe_memory_data_1_data), .out(d0), .sel(MD0));
  Multiplexer #(.width(8)) multiplexer_28 (.in0(vpe_ula_2_out_4), .in1(vpe_memory_data_2_data), .out(d1), .sel(MD1));
  Multiplexer #(.width(8)) multiplexer_29 (.in0(vpe_ula_3_out_4), .in1(vpe_memory_data_3_data), .out(d2), .sel(MD2));
  Multiplexer #(.width(8)) multiplexer_30 (.in0(vpe_ula_4_out_4), .in1(vpe_memory_data_4_data), .out(d3), .sel(MD3));
  SPE_Memory_Data spe_memory_data_1 (.Addr(RB), .WM(W), .Clk(Clk), .d(RA), .data(spe_memory_data_1_data));
  Multiplexer #(.width(8)) multiplexer_31 (.in0(spe_ula_1_out_4), .in1(spe_memory_data_1_data), .out(Data), .sel(MD));

  // Notes on the sheet:
  //   Register bank's control signs
  //   =============================== Vector Processing Element ===============================
  //   ALU's control signs
  //   =============================== Scalar Processing Element ===============================
  //   =============================== Scalar Processing Element ===============================
  //   Register bank's control signs
endmodule

module Program_Counter (
  input  [7:0] PC_P,
  input  Clk,
  input  R,
  output [7:0] PC_N
);

  Register register_1 (.D(PC_P), .en(1'b1), .clk(Clk), .Q(PC_N), .clr(R));
endmodule

module Memory_Instruction (
  input  [7:0] Addr_PC,
  output [7:0] Inst
);

  ROM rom_1 (.addr(Addr_PC), .data(Inst));

  // Notes on the sheet:
  //   contents of rom_1 (hex, n*v repeats v):
  //   40 34 14 8 74 55 74 40 40 40
endmodule

module Control_Unit (
  input  [3:0] Opcode,
  output Vec,
  output WE,
  output RadSpe,
  output [2:0] UlaOpSpe,
  output [1:0] UlaSrSpe,
  output BrSpe,
  output MD,
  output WM,
  output [6:0] VecSg
);

  ROM #(.addrWidth(4), .dataWidth(18)) rom_1 (
    .addr(Opcode), .data({Vec, WE, RadSpe, UlaOpSpe, UlaSrSpe, BrSpe, MD, WM, VecSg}));

  // Notes on the sheet:
  //   contents of rom_1 (hex, n*v repeats v):
  //   202 1 308 328 240 260 280 14 8*400
endmodule

module SPE_Register_Bank (
  input  [7:0] Data,
  input  [1:0] RA,
  input  WE,
  input  [1:0] RD,
  input  [1:0] RB,
  input  Clk,
  input  R,
  output [7:0] RD1,
  output [7:0] RD2
);

  wire demultiplexer_1_out0, R1, R2, R3;
  wire [7:0] D1, D2, D3;

  // NoConnect on demultiplexer_1_out0
  Demultiplexer #(.select(2)) demultiplexer_1 (
    .out0(demultiplexer_1_out0), .out1(R1), .out2(R2), .out3(R3), .in(WE), .sel(RD));
  Register u_R1 (.D(Data), .en(R1), .clk(Clk), .Q(D1), .clr(R));
  Register u_R2 (.D(Data), .en(R2), .clk(Clk), .Q(D2), .clr(R));
  Register u_R3 (.D(Data), .en(R3), .clk(Clk), .Q(D3), .clr(R));
  Multiplexer #(.select(2), .width(8)) multiplexer_1 (
    .in0({8{1'b0}}), .in1(D1), .in2(D2), .in3(D3), .out(RD1), .sel(RA));
  Multiplexer #(.select(2), .width(8)) multiplexer_2 (
    .in0({8{1'b0}}), .in1(D1), .in2(D2), .in3(D3), .out(RD2), .sel(RB));

  // Notes on the sheet:
  //   R0
endmodule

module SPE_ULA (
  input  [7:0] RA,
  input  [7:0] RB,
  input  [2:0] ULA_Op,
  output [7:0] out_4,
  output Zero
);

  wire [7:0] R2, R3, R4;

  // NoConnect on RA[7:4]
  // NoConnect on RB[7:4]
  // NoConnect on RB[7:4]
  // NoConnect on RA[3:0]
  Adder adder_1 (.a(RA), .b(RB), .out(R2));  // open: cin, cout
  Subtractor subtractor_1 (.a(RA), .b(RB), .out(R3));  // open: bin, bout
  assign R4 = RA & RB;  // AND_Gate and_1, 8 bits wide
  Multiplexer #(.select(3), .width(8)) multiplexer_1 (
    .in0({RB[3:0], RA[3:0]}), .in1({RA[7:4], RB[3:0]}), .in2(R2), .in3(R3), .in4(R4), .in5({8{1'b0}}),
    .in6({8{1'b0}}), .in7({8{1'b0}}), .out(out_4), .sel(ULA_Op));
  nor nor_1 (Zero, R3[0], R3[1], R3[2], R3[3], R3[4], R3[5], R3[6], R3[7]);

  // Other names for the same wires on the sheet: R0[7:0] = {RB[3:0], RA[3:0]}; R1[7:0] = {RA[7:4], RB[3:0]}

  // Notes on the sheet:
  //   Move High
  //   Move Low
  //   Adder
  //   Subtractor
  //   AND
endmodule

module SPE_Memory_Data (
  input  [7:0] Addr,
  input  WM,
  input  Clk,
  input  [7:0] d,
  output [7:0] data
);

  RAM ram_1 (.addr(Addr), .we(WM), .oe(1'b1), .clk(Clk), .din(d), .dout(data));
endmodule

module VPE_Ctrl (
  input  [6:0] VectorSigns,
  output [1:0] ID_V,
  output [2:0] EXE_V,
  output [1:0] MEM_V
);


  assign EXE_V = VectorSigns[4:2];
  assign ID_V = VectorSigns[1:0];
  assign MEM_V = VectorSigns[6:5];
endmodule

module VPE0_Register_Bank (
  input  [7:0] Data,
  input  [1:0] RA,
  input  WE,
  input  [1:0] RD,
  input  [1:0] RB,
  input  Clk,
  input  R,
  output [7:0] RD1,
  output [7:0] RD2
);

  wire demultiplexer_1_out0, R1, R2, R3;
  wire [7:0] D1, D2, D3;

  // NoConnect on demultiplexer_1_out0
  Demultiplexer #(.select(2)) demultiplexer_1 (
    .out0(demultiplexer_1_out0), .out1(R1), .out2(R2), .out3(R3), .in(WE), .sel(RD));
  Register VR1 (.D(Data), .en(R1), .clk(Clk), .Q(D1), .clr(R));
  Register VR2 (.D(Data), .en(R2), .clk(Clk), .Q(D2), .clr(R));
  Register VR4 (.D(Data), .en(R3), .clk(Clk), .Q(D3), .clr(R));
  Multiplexer #(.select(2), .width(8)) multiplexer_1 (
    .in0({8{1'b0}}), .in1(D1), .in2(D2), .in3(D3), .out(RD1), .sel(RA));
  Multiplexer #(.select(2), .width(8)) multiplexer_2 (
    .in0({8{1'b0}}), .in1(D1), .in2(D2), .in3(D3), .out(RD2), .sel(RB));

  // Notes on the sheet:
  //   VR0
endmodule

module VPE1_Register_Bank (
  input  [7:0] Data,
  input  [1:0] RA,
  input  WE,
  input  [1:0] RD,
  input  [1:0] RB,
  input  Clk,
  input  R,
  output [7:0] RD1,
  output [7:0] RD2
);

  wire demultiplexer_1_out0, R1, R2, R3;
  wire [7:0] D1, D2, D3;

  // NoConnect on demultiplexer_1_out0
  Demultiplexer #(.select(2)) demultiplexer_1 (
    .out0(demultiplexer_1_out0), .out1(R1), .out2(R2), .out3(R3), .in(WE), .sel(RD));
  Register VR1 (.D(Data), .en(R1), .clk(Clk), .Q(D1), .clr(R));
  Register VR2 (.D(Data), .en(R2), .clk(Clk), .Q(D2), .clr(R));
  Register VR4 (.D(Data), .en(R3), .clk(Clk), .Q(D3), .clr(R));
  Multiplexer #(.select(2), .width(8)) multiplexer_1 (.in0(8'h1), .in1(D1), .in2(D2), .in3(D3), .out(RD1), .sel(RA));
  Multiplexer #(.select(2), .width(8)) multiplexer_2 (.in0(8'h1), .in1(D1), .in2(D2), .in3(D3), .out(RD2), .sel(RB));

  // Notes on the sheet:
  //   VR0
endmodule

module VPE2_Register_Bank (
  input  [7:0] Data,
  input  [1:0] RA,
  input  WE,
  input  [1:0] RD,
  input  [1:0] RB,
  input  Clk,
  input  R,
  output [7:0] RD1,
  output [7:0] RD2
);

  wire demultiplexer_1_out0, R1, R2, R3;
  wire [7:0] D1, D2, D3;

  // NoConnect on demultiplexer_1_out0
  Demultiplexer #(.select(2)) demultiplexer_1 (
    .out0(demultiplexer_1_out0), .out1(R1), .out2(R2), .out3(R3), .in(WE), .sel(RD));
  Register VR1 (.D(Data), .en(R1), .clk(Clk), .Q(D1), .clr(R));
  Register VR2 (.D(Data), .en(R2), .clk(Clk), .Q(D2), .clr(R));
  Register VR4 (.D(Data), .en(R3), .clk(Clk), .Q(D3), .clr(R));
  Multiplexer #(.select(2), .width(8)) multiplexer_1 (.in0(8'h2), .in1(D1), .in2(D2), .in3(D3), .out(RD1), .sel(RA));
  Multiplexer #(.select(2), .width(8)) multiplexer_2 (.in0(8'h2), .in1(D1), .in2(D2), .in3(D3), .out(RD2), .sel(RB));

  // Notes on the sheet:
  //   VR0
endmodule

module VPE3_Register_Bank (
  input  [7:0] Data,
  input  [1:0] RA,
  input  WE,
  input  [1:0] RD,
  input  [1:0] RB,
  input  Clk,
  input  R,
  output [7:0] RD1,
  output [7:0] RD2
);

  wire demultiplexer_1_out0, R1, R2, R3;
  wire [7:0] D1, D2, D3;

  // NoConnect on demultiplexer_1_out0
  Demultiplexer #(.select(2)) demultiplexer_1 (
    .out0(demultiplexer_1_out0), .out1(R1), .out2(R2), .out3(R3), .in(WE), .sel(RD));
  Register VR1 (.D(Data), .en(R1), .clk(Clk), .Q(D1), .clr(R));
  Register VR2 (.D(Data), .en(R2), .clk(Clk), .Q(D2), .clr(R));
  Register VR4 (.D(Data), .en(R3), .clk(Clk), .Q(D3), .clr(R));
  Multiplexer #(.select(2), .width(8)) multiplexer_1 (.in0(8'h3), .in1(D1), .in2(D2), .in3(D3), .out(RD1), .sel(RA));
  Multiplexer #(.select(2), .width(8)) multiplexer_2 (.in0(8'h3), .in1(D1), .in2(D2), .in3(D3), .out(RD2), .sel(RB));

  // Notes on the sheet:
  //   VR0
endmodule

module VPE_ULA (
  input  [7:0] RA,
  input  [7:0] RB,
  input  [1:0] ULA_Op,
  output [7:0] out_4
);

  wire [7:0] R2, R3;

  // NoConnect on RA[7:4]
  // NoConnect on RB[7:4]
  // NoConnect on RB[7:4]
  // NoConnect on RA[3:0]
  Adder adder_1 (.a(RA), .b(RB), .out(R2));  // open: cin, cout
  Subtractor subtractor_1 (.a(RA), .b(RB), .out(R3));  // open: bin, bout
  Multiplexer #(.select(2), .width(8)) multiplexer_1 (
    .in0({RB[3:0], RA[3:0]}), .in1({RA[7:4], RB[3:0]}), .in2(R2), .in3(R3), .out(out_4), .sel(ULA_Op));

  // Other names for the same wires on the sheet: R0[7:0] = {RB[3:0], RA[3:0]}; R1[7:0] = {RA[7:4], RB[3:0]}

  // Notes on the sheet:
  //   Move High
  //   Move Low
  //   Adder
  //   Subtractor
endmodule

module VPE_Memory_Data (
  input  [7:0] Addr,
  input  WM,
  input  Clk,
  input  [7:0] d,
  output [7:0] data
);

  RAM ram_1 (.addr(Addr), .we(WM), .oe(1'b1), .clk(Clk), .din(d), .dout(data));
endmodule
