// Logisim project t2v0.circ as structural Verilog: 4 circuits, main circuit main
module main (
  output [1:0] out_1,
  output [7:0] inst,
  output [7:0] out_3,
  output [7:0] out_4,
  output [1:0] out_5,
  output [7:0] out_6,
  output [7:0] out_7,
  output [3:0] opcode,
  output [7:0] out_9
);

  wire and_1_out, branchOK, brzrOK, clk, ji, JIJR, or_1_out, or_2_out, reset, SelBranch, selR0, ULAsrc, WBR,
       WDU, WMD;
  wire [1:0] multiplexer_5_out;
  wire [3:0] ULAop;
  wire [7:0] adder_1_out, branch, multiplexer_1_out, multiplexer_2_out, multiplexer_3_out, multiplexer_4_out,
       multiplexer_7_out;

  Multiplexer #(.width(8)) multiplexer_1 (.in0(8'h1), .in1(out_6), .out(multiplexer_1_out), .sel(ji));
  and and_1 (and_1_out, brzrOK, branchOK);
  Button u_reset (.out(reset));
  Adder adder_1 (.a(multiplexer_1_out), .b(inst), .out(adder_1_out));  // open: cin, cout
  or or_1 (or_1_out, JIJR, and_1_out);
  Multiplexer #(.width(8)) multiplexer_2 (.in0(adder_1_out), .in1(branch), .out(multiplexer_2_out), .sel(or_1_out));
  Register PC (.D(multiplexer_2_out), .en(1'b1), .clk(clk), .Q(inst), .clr(reset));
  or or_2 (or_2_out, WMD, clk);
  Multiplexer #(.width(8)) multiplexer_3 (.in0(out_7), .in1(out_9), .out(multiplexer_3_out), .sel(WDU));
  Clock clock_1 (.out(clk));
  Multiplexer #(.width(8)) multiplexer_4 (.in0(out_3), .in1(inst), .out(multiplexer_4_out), .sel(clk));
  RAM #(.asyncread("true")) ram_1 (
    .addr(multiplexer_4_out), .we(or_2_out), .oe(1'b1), .clk(clk), .din(out_4), .dout(out_9));
  Multiplexer #(.width(2)) multiplexer_5 (.in0(out_1), .in1(2'b00), .out(multiplexer_5_out), .sel(selR0));
  Register #(.trigger("falling")) pcbuf (.D(out_9), .en(1'b1), .clk(clk), .Q({opcode, out_1, out_5}), .clr(reset));
  BancoReg bancoreg_1 (
    .clk(clk), .d(multiplexer_3_out), .w(WBR), .SelW(multiplexer_5_out), .SelA(multiplexer_5_out),
    .SelB(out_5), .reset(reset), .A(out_4), .B(out_3));
  extSinal extsinal_1 (.imm4({out_1, out_5}), .imm8(out_6));
  Multiplexer #(.width(8)) multiplexer_6 (.in0(out_3), .in1(out_6), .out(branch), .sel(SelBranch));
  Multiplexer #(.width(8)) multiplexer_7 (.in0(out_3), .in1(out_6), .out(multiplexer_7_out), .sel(ULAsrc));
  ROM #(.addrWidth(4), .dataWidth(13)) rom_1 (
    .addr(opcode), .data({ji, WDU, WBR, WMD, ULAsrc, ULAop, SelBranch, branchOK, JIJR, selR0}));
  ULA ula_1 (.A(out_4), .B(multiplexer_7_out), .Seletor(ULAop), .brzr(brzrOK), .R(out_7));

  // Other names for the same wires on the sheet: inst_t[7:0] = {opcode, out_1, out_5}; A[7:0] = out_4; B[7:0] = out_3;
  //   imm8[7:0] = out_6; imm4[3:0] = {out_1, out_5}; rb[1:0] = out_5; ra[1:0] = out_1; memdata[7:0] = out_9;
  //   saidaPC[7:0] = inst; ULAdata[7:0] = out_7

  // Notes on the sheet:
  //   Mudar selBranch, talvez nao precise
  //   regist
  //   dados
  //   Mem de Inst e Dados
  //   salto ou st ld
  //   contents of rom_1 (hex, n*v repeats v):
  //   34 114a c48 248 541 571 468 42 408 418 428 438 448 458 488 498
  //   Mem de Controle
endmodule

module ULA (
  input  [7:0] A,
  input  [7:0] B,
  input  [3:0] Seletor,
  output brzr,
  output [7:0] R
);

  wire [0:0] R0;
  wire [7:0] R1, R2, R3, R4, R5, R6, R7, R8, R9;

  Multiplexer #(.select(4), .width(8)) multiplexer_1 (
    .in0({{7{1'b0}}, R0[0]}), .in1(R1), .in2(R2), .in3(R3), .in4(R4), .in5(R5), .in6(R6), .in7(R7), .in8(R8),
    .in9(R9), .out(R), .sel(Seletor));  // open: in10, in11, in12, in13, in14, in15
  assign R1 = A & B;  // AND_Gate and_1, 8 bits wide
  assign R2 = A | B;  // OR_Gate or_1, 8 bits wide
  assign R3 = A ^ B;  // XOR_Gate xor_1, 8 bits wide
  nor nor_1 (R0[0], B[0], B[1], B[2], B[3], B[4], B[5], B[6], B[7]);
  Adder adder_1 (.a(A), .b(B), .out(R4));  // open: cin, cout
  Subtractor subtractor_1 (.a(A), .b(B), .out(R5));  // open: bin, bout
  Subtractor subtractor_2 (.a(A), .b(8'h1), .out(R6));  // open: bin, bout
  Multiplier multiplier_1 (.a(A), .b(B), .out(R7));  // open: cin, cout
  Shifter shifter_1 (.in(A), .\dist (B[2:0]), .out(R8));
  Shifter #(.shift("lr")) shifter_2 (.in(A), .\dist (B[2:0]), .out(R9));
  Comparator comparator_1 (.a(A), .b({8{1'b0}}), .eq(brzr));  // open: gt, lt

  // Notes on the sheet:
  //   Add
  //   Sub
  //   Dec
  //   Mult
  //   Slr
  //   Srr
endmodule

module BancoReg (
  input  clk,
  input  [7:0] d,
  input  w,
  input  [1:0] SelW,
  input  [1:0] SelA,
  input  [1:0] SelB,
  input  reset,
  output [7:0] A,
  output [7:0] B
);

  wire w0, w1, w2, w3;
  wire [7:0] l0, l1, l2, l3;

  Demultiplexer #(.select(2)) demultiplexer_1 (.out0(w0), .out1(w1), .out2(w2), .out3(w3), .in(w), .sel(SelW));
  Multiplexer #(.select(2), .width(8)) multiplexer_1 (.in0(l0), .in1(l1), .in2(l2), .in3(l3), .out(A), .sel(SelA));
  Multiplexer #(.select(2), .width(8)) multiplexer_2 (.in0(l0), .in1(l1), .in2(l2), .in3(l3), .out(B), .sel(SelB));
  Register r0 (.D(d), .en(w0), .clk(clk), .Q(l0), .clr(reset));
  Register r1 (.D(d), .en(w1), .clk(clk), .Q(l1), .clr(reset));
  Register r2 (.D(d), .en(w2), .clk(clk), .Q(l2), .clr(reset));
  Register r3 (.D(d), .en(w3), .clk(clk), .Q(l3), .clr(reset));

  // Other names for the same wires on the sheet: data[7:0] = d

  // Notes on the sheet:
  //   Escrita
  //   Leitura A
  //   Leitura B
endmodule

module extSinal (
  input  [3:0] imm4,
  output [7:0] imm8
);


  assign imm8 = {{5{imm4[3]}}, imm4[2:0]};
endmodule
