// Logisim project Sagui_Vetorial.circ as structural Verilog: 18 circuits, main circuit main
module main (
);

  wire Br, Clk, control_unit_1_p2, control_unit_1_p3, control_unit_1_p4, control_unit_1_p5,
       control_unit_1_p6, control_unit_1_p7, control_unit_1_p8, control_unit_1_p9, IsBr, MD, Nop, R, RAD,
       spe_ula_1_zero, V_MD, V_MRd, V_MSti, V_RAD, V_USr, V_WE, V_WM, W, WE;
  wire [1:0] ID, MEM, multiplexer_2_out, multiplexer_4_out, multiplexer_5_out, multiplexer_7_out,
       multiplexer_8_out, multiplexer_10_out, multiplexer_11_out, multiplexer_13_out, multiplexer_14_out,
       RA_ID, RB_ID, USr, V_Mem;
  wire [2:0] UOp, V_UOp;
  wire [3:0] Opcode, V_Exe, V_Id;
  wire [5:0] EXE;
  wire [7:0] adder_1_out, d0, d1, d2, d3, Data, imm, memory_instruction_1_inst, multiplexer_1_out,
       multiplexer_6_out, multiplexer_9_out, multiplexer_12_out, multiplexer_15_out, multiplexer_17_out,
       multiplexer_18_out, multiplexer_19_out, multiplexer_20_out, multiplexer_22_out, N_Ptr0, N_Ptr1,
       N_Ptr2, N_Ptr3, program_counter_1_pc_n, RA, RA0, RA1, RA2, RA3, RB, RB0, RB1, RB2, RB3,
       spe_memory_data_1_data, spe_register_bank_1_rd1, spe_register_bank_1_rd2, spe_ula_1_out_4, undriven,
       vpe_memory_data_1_data, vpe_memory_data_2_data, vpe_memory_data_3_data, vpe_memory_data_4_data,
       vpe_ula_1_out_4, vpe_ula_2_out_4, vpe_ula_3_out_4, vpe_ula_4_out_4;
  wire [9:0] VS;

  Multiplexer #(.width(8)) multiplexer_1 (.in0(adder_1_out), .in1(RB), .out(multiplexer_1_out), .sel(IsBr));
  Program_Counter program_counter_1 (.PC_P(multiplexer_1_out), .Clk(Clk), .R(R), .PC_N(program_counter_1_pc_n));
  Clock clock_1 (.out(Clk));
  Button Reset (.out(R));
  Adder adder_1 (.a(program_counter_1_pc_n), .b(8'h1), .out(adder_1_out));  // open: cin, cout
  Memory_Instruction memory_instruction_1 (.Addr_PC(program_counter_1_pc_n), .Inst(memory_instruction_1_inst));
  Stg_IF_ID stg_if_id_1 (.Inst_IF(memory_instruction_1_inst), .Inst_ID({Opcode, RA_ID, RB_ID}));  // open: Clk, R
  Multiplexer #(.width(2)) multiplexer_2 (.in0(RA_ID), .in1(2'b01), .out(multiplexer_2_out), .sel(RAD));
  VPE_Ctrl vpe_ctrl_1 (.VectorSigns(VS), .ID_V(V_Id), .EXE_V(V_Exe), .MEM_V(V_Mem));
  Multiplexer #(.width(2)) multiplexer_3 (.in0(ID), .in1(2'b00), .out({RAD, WE}), .sel(Nop));
  assign imm = {{4{RA_ID[1]}}, {RA_ID, RB_ID}};  // Bit_Extender bit_extender_1
  Multiplexer #(.width(2)) multiplexer_4 (.in0(RA_ID), .in1(2'b01), .out(multiplexer_4_out), .sel(V_RAD));
  Multiplexer #(.width(2)) multiplexer_5 (.in0(multiplexer_4_out), .in1(RB_ID), .out(multiplexer_5_out), .sel(V_MRd));
  Multiplexer #(.width(8)) multiplexer_6 (.in0(d0), .in1(N_Ptr0), .out(multiplexer_6_out), .sel(V_MSti));
  Multiplexer #(.width(2)) multiplexer_7 (.in0(RA_ID), .in1(2'b01), .out(multiplexer_7_out), .sel(V_RAD));
  Multiplexer #(.width(2)) multiplexer_8 (.in0(multiplexer_7_out), .in1(RB_ID), .out(multiplexer_8_out), .sel(V_MRd));
  Multiplexer #(.width(8)) multiplexer_9 (.in0(d1), .in1(N_Ptr1), .out(multiplexer_9_out), .sel(V_MSti));
  Multiplexer #(.width(2)) multiplexer_10 (.in0(RA_ID), .in1(2'b01), .out(multiplexer_10_out), .sel(V_RAD));
  Multiplexer #(.width(2)) multiplexer_11 (
    .in0(multiplexer_10_out), .in1(RB_ID), .out(multiplexer_11_out), .sel(V_MRd));
  Multiplexer #(.width(8)) multiplexer_12 (.in0(d2), .in1(N_Ptr2), .out(multiplexer_12_out), .sel(V_MSti));
  Multiplexer #(.width(2)) multiplexer_13 (.in0(RA_ID), .in1(2'b01), .out(multiplexer_13_out), .sel(V_RAD));
  Multiplexer #(.width(2)) multiplexer_14 (
    .in0(multiplexer_13_out), .in1(RB_ID), .out(multiplexer_14_out), .sel(V_MRd));
  Multiplexer #(.width(8)) multiplexer_15 (.in0(d3), .in1(N_Ptr3), .out(multiplexer_15_out), .sel(V_MSti));
  SPE_Register_Bank spe_register_bank_1 (
    .WE(WE), .Data(Data), .RD(multiplexer_2_out), .Clk(Clk), .R(R), .RA(multiplexer_2_out), .RB(RB_ID),
    .RD1(spe_register_bank_1_rd1), .RD2(spe_register_bank_1_rd2));
  // Control_Unit control_unit_1: pin names not known; wires that end beside it: Opcode, control_unit_1_p2, control_unit_1_p3, control_unit_1_p4, control_unit_1_p5, control_unit_1_p6, control_unit_1_p7, control_unit_1_p8, control_unit_1_p9, Nop, VS
  Multiplexer #(.width(4)) multiplexer_16 (.in0(4'b0000), .in1(V_Id), .out({V_WE, V_RAD, V_MSti, V_MRd}), .sel(Nop));
  VPE0_Register_Bank vpe0_register_bank_1 (
    .WE(V_WE), .Data(multiplexer_6_out), .RD(multiplexer_5_out), .Clk(Clk), .R(R), .RA(multiplexer_4_out),
    .RB(RB_ID), .RD1(RA0), .RD2(RB0));
  VPE1_Register_Bank vpe1_register_bank_1 (
    .WE(V_WE), .Data(multiplexer_9_out), .RD(multiplexer_8_out), .Clk(Clk), .R(R), .RA(multiplexer_7_out),
    .RB(RB_ID), .RD1(RA1), .RD2(RB1));
  VPE2_Register_Bank vpe2_register_bank_1 (
    .WE(V_WE), .Data(multiplexer_12_out), .RD(multiplexer_11_out), .Clk(Clk), .R(R), .RA(multiplexer_10_out),
    .RB(RB_ID), .RD1(RA2), .RD2(RB2));
  VPE3_Register_Bank vpe3_register_bank_1 (
    .WE(V_WE), .Data(multiplexer_15_out), .RD(multiplexer_14_out), .Clk(Clk), .R(R), .RA(multiplexer_13_out),
    .RB(RB_ID), .RD1(RA3), .RD2(RB3));
  Multiplexer #(.width(8)) multiplexer_17 (.in0(RB0), .in1(imm), .out(multiplexer_17_out), .sel(V_USr));
  Multiplexer #(.width(8)) multiplexer_18 (.in0(RB1), .in1(imm), .out(multiplexer_18_out), .sel(V_USr));
  Multiplexer #(.width(8)) multiplexer_19 (.in0(RB2), .in1(imm), .out(multiplexer_19_out), .sel(V_USr));
  Multiplexer #(.width(8)) multiplexer_20 (.in0(RB3), .in1(imm), .out(multiplexer_20_out), .sel(V_USr));
  Stg_ID_EX_Spe stg_id_ex_spe_1 ();  // open: Imm_Id, ExeSgn_Id, MemSgn_Id, WbSgn_Id, RD1_Id, RD2_Id, ARs_Id, Clk, R, Imm_Exe, ExeSgn_Exe, MemSgn_Exe, WbSgn_Exe, RD1_Exe, RD2_Exe, ARs_Exe
  Multiplexer #(.width(4)) multiplexer_21 (.in0(4'b0000), .in1(V_Exe), .out({V_USr, V_UOp}), .sel(Nop));
  Multiplexer #(.select(2), .width(8)) multiplexer_22 (
    .in0(RB), .in2({8{1'b0}}), .in3({8{1'b0}}), .out(multiplexer_22_out), .sel(USr));  // open: in1
  VPE_ULA vpe_ula_1 (.ULA_Op(V_UOp), .RA(RA0), .RB(multiplexer_17_out), .out_4(vpe_ula_1_out_4));
  VPE_ULA vpe_ula_2 (.ULA_Op(V_UOp), .RA(RA1), .RB(multiplexer_18_out), .out_4(vpe_ula_2_out_4));
  VPE_ULA vpe_ula_3 (.ULA_Op(V_UOp), .RA(RA2), .RB(multiplexer_19_out), .out_4(vpe_ula_3_out_4));
  VPE_ULA vpe_ula_4 (.ULA_Op(V_UOp), .RA(RA3), .RB(multiplexer_20_out), .out_4(vpe_ula_4_out_4));
  Multiplexer #(.width(6)) multiplexer_23 (.in0(EXE), .in1({6{1'b0}}), .out({Br, USr, UOp}), .sel(Nop));
  Multiplexer #(.width(2)) multiplexer_24 (.in0(2'b00), .in1(V_Mem), .out({V_WM, V_MD}), .sel(Nop));
  Adder adder_2 (.a(8'h4), .b(RB0), .out(N_Ptr0));  // open: cin, cout
  Adder adder_3 (.a(8'h4), .b(RB1), .out(N_Ptr1));  // open: cin, cout
  Adder adder_4 (.a(8'h4), .b(RB2), .out(N_Ptr2));  // open: cin, cout
  Adder adder_5 (.a(8'h4), .b(RB3), .out(N_Ptr3));  // open: cin, cout
  SPE_ULA spe_ula_1 (.ULA_Op(UOp), .RA(RA), .RB(multiplexer_22_out), .out_4(spe_ula_1_out_4), .Zero(spe_ula_1_zero));
  VPE_Memory_Data vpe_memory_data_1 (.Addr(RB0), .WM(V_WM), .Clk(Clk), .d(RA0), .data(vpe_memory_data_1_data));
  VPE_Memory_Data vpe_memory_data_2 (.Addr(RB1), .WM(V_WM), .Clk(Clk), .d(RA1), .data(vpe_memory_data_2_data));
  VPE_Memory_Data vpe_memory_data_3 (.Addr(RB2), .WM(V_WM), .Clk(Clk), .d(RA2), .data(vpe_memory_data_3_data));
  VPE_Memory_Data vpe_memory_data_4 (.Addr(RB3), .WM(V_WM), .Clk(Clk), .d(RA3), .data(vpe_memory_data_4_data));
  and and_1 (IsBr, Br, spe_ula_1_zero);
  Multiplexer #(.width(8)) multiplexer_25 (.in0(vpe_ula_1_out_4), .in1(vpe_memory_data_1_data), .out(d0), .sel(V_MD));
  Multiplexer #(.width(8)) multiplexer_26 (.in0(vpe_ula_2_out_4), .in1(vpe_memory_data_2_data), .out(d1), .sel(V_MD));
  Multiplexer #(.width(8)) multiplexer_27 (.in0(vpe_ula_3_out_4), .in1(vpe_memory_data_3_data), .out(d2), .sel(V_MD));
  Multiplexer #(.width(8)) multiplexer_28 (.in0(vpe_ula_4_out_4), .in1(vpe_memory_data_4_data), .out(d3), .sel(V_MD));
  Stg_EX_MEM_Spe stg_ex_mem_spe_1 (.UlaR_Exe(spe_ula_1_out_4));  // open: AddrR_Exe, MemSgn_Exe, WbSgn_Exe, Addr_Exe, Data_Exe, Clk, R, AddrR_Mem, MemSgn_Mem, WbSgn_Mem, UlaR_Mem, Addr_Mem, Data_Mem
  Multiplexer #(.width(2)) multiplexer_29 (.in0(MEM), .in1(2'b00), .out({W, MD}), .sel(Nop));
  Multiplexer #(.width(8)) multiplexer_30 (.in0(undriven), .in1(spe_memory_data_1_data), .out(Data), .sel(MD));
  SPE_Memory_Data spe_memory_data_1 (.Addr(RB), .WM(W), .Clk(Clk), .d(RA), .data(spe_memory_data_1_data));
  Stg_MEM_WB_Spe stg_mem_wb_spe_1 ();  // open: AddrR_Exe, WbSgn_Exe, Data_Exe, Clk, R, AddrR_Mem, WbSgn_Mem, Data_Mem

  // Notes on the sheet:
  //   VPE: control signs
  //   Register bank's control signs
  //   VPE: Register bank's control signs
  //   =============================== Vector Processing Element ===============================
  //   =============================== Scalar Processing Element ===============================
  //   VPE: ALU's control signs
  //   ================== VPE0 ==================
  //   ================== VPE1 ==================
  //   ================== VPE2 ==================
  //   ================== VPE3 ==================
  //   ALU's control signs
  //   VPE: Memory's control signs
  //   Next address
  //   Next address
  //   Next address
  //   Next address
  //   Register bank's control signs
endmodule

module Program_Counter (
  input  [7:0] PC_P,
  input  Clk,
  input  R,
  output [7:0] PC_N
);

  Register PC (.D(PC_P), .en(1'b1), .clk(Clk), .Q(PC_N), .clr(R));
endmodule

module Memory_Instruction (
  input  [7:0] Addr_PC,
  output [7:0] Inst
);

  ROM rom_1 (.addr(Addr_PC), .data(Inst));

  // Notes on the sheet:
  //   contents of rom_1 (hex, n*v repeats v):
  //   c8 cc b4 32 49 ee 3d 79 cd 31 59 35 71 32 49 bc cd b4 ee 21 3d 79 cd 20 31 59 21 32 71 55 32 49 b0
  //   e6 22 3b 79 20 31 59 22 31 71 55 32 49 da c8 8e a0 bc c9 86 cd a0 bc c9 9e 24 36 79 20 31 59 a1 b4
  //   d9 23 30 71 70
endmodule

module Control_Unit (
  input  [3:0] Opcode,
  output Vec,
  output WESpe,
  output RadSpe,
  output [2:0] UlaOpSpe,
  output [1:0] UlaSrSpe,
  output BrSpe,
  output MDSpe,
  output WMSpe,
  output [9:0] VecSg
);

  ROM #(.addrWidth(4), .dataWidth(21)) rom_1 (
    .addr(Opcode), .data({Vec, WESpe, RadSpe, UlaOpSpe, UlaSrSpe, BrSpe, MDSpe, WMSpe, VecSg}));

  // Notes on the sheet:
  //   contents of rom_1 (hex, n*v repeats v):
  //   80800 400 c2000 ca000 90000 98000 a0000 5000 100202 100001 100304 10030c 100210 100218 1002c1 100220
  //   Total de bits: 21
  //   0..9: signs of the vector part
  //   10..20: signs of the scalar part
  //   21: control bit between scalar and vector instructions
endmodule

module SPE_Register_Bank (
  input  [7:0] Data,
  input  [1:0] RA,
  input  WE,
  input  [1:0] RD,
  input  [1:0] RB,
  input  Clk,
  input  R,
  output [7:0] RD1,
  output [7:0] RD2
);

  wire demultiplexer_1_out0, R1, R2, R3;
  wire [7:0] D1, D2, D3;

  // NoConnect on demultiplexer_1_out0
  Demultiplexer #(.select(2)) demultiplexer_1 (
    .out0(demultiplexer_1_out0), .out1(R1), .out2(R2), .out3(R3), .in(WE), .sel(RD));
  Register SR1 (.D(Data), .en(R1), .clk(Clk), .Q(D1), .clr(R));
  Register SR2 (.D(Data), .en(R2), .clk(Clk), .Q(D2), .clr(R));
  Register SR3 (.D(Data), .en(R3), .clk(Clk), .Q(D3), .clr(R));
  Multiplexer #(.select(2), .width(8)) multiplexer_1 (
    .in0({8{1'b0}}), .in1(D1), .in2(D2), .in3(D3), .out(RD1), .sel(RA));
  Multiplexer #(.select(2), .width(8)) multiplexer_2 (
    .in0({8{1'b0}}), .in1(D1), .in2(D2), .in3(D3), .out(RD2), .sel(RB));

  // Notes on the sheet:
  //   SR0
endmodule

module SPE_ULA (
  input  [7:0] RA,
  input  [7:0] RB,
  input  [2:0] ULA_Op,
  output [7:0] out_4,
  output Zero
);

  wire [7:0] R2, R3, R4;

  // NoConnect on RA[7:4]
  // NoConnect on RB[7:4]
  // NoConnect on RB[7:4]
  // NoConnect on RA[3:0]
  Adder adder_1 (.a(RA), .b(RB), .out(R2));  // open: cin, cout
  Subtractor subtractor_1 (.a(RA), .b(RB), .out(R3));  // open: bin, bout
  assign R4 = RA & RB;  // AND_Gate and_1, 8 bits wide
  Multiplexer #(.select(3), .width(8)) multiplexer_1 (
    .in0({RB[3:0], RA[3:0]}), .in1({RA[7:4], RB[3:0]}), .in2(R2), .in3(R3), .in4(R4), .in5({8{1'b0}}),
    .in6({8{1'b0}}), .in7({8{1'b0}}), .out(out_4), .sel(ULA_Op));
  nor nor_1 (Zero, R3[0], R3[1], R3[2], R3[3], R3[4], R3[5], R3[6], R3[7]);

  // Other names for the same wires on the sheet: R0[7:0] = {RB[3:0], RA[3:0]}; R1[7:0] = {RA[7:4], RB[3:0]}

  // Notes on the sheet:
  //   Move High
  //   Move Low
  //   Adder
  //   Subtractor
  //   AND
endmodule

module SPE_Memory_Data (
  input  [7:0] Addr,
  input  WM,
  input  Clk,
  input  [7:0] d,
  output [7:0] data
);

  RAM ram_1 (.addr(Addr), .we(WM), .oe(1'b1), .clk(Clk), .din(d), .dout(data));
endmodule

module VPE_Ctrl (
  input  [9:0] VectorSigns,
  output [3:0] ID_V,
  output [3:0] EXE_V,
  output [1:0] MEM_V
);


  assign EXE_V = {VectorSigns[2], VectorSigns[5:3]};
  assign ID_V = VectorSigns[9:6];
  assign MEM_V = {VectorSigns[0], VectorSigns[1]};
endmodule

module VPE0_Register_Bank (
  input  [7:0] Data,
  input  [1:0] RA,
  input  WE,
  input  [1:0] RD,
  input  [1:0] RB,
  input  Clk,
  input  R,
  output [7:0] RD1,
  output [7:0] RD2
);

  wire demultiplexer_1_out0, R1, R2, R3;
  wire [7:0] D1, D2, D3;

  // NoConnect on demultiplexer_1_out0
  Demultiplexer #(.select(2)) demultiplexer_1 (
    .out0(demultiplexer_1_out0), .out1(R1), .out2(R2), .out3(R3), .in(WE), .sel(RD));
  Register VR1 (.D(Data), .en(R1), .clk(Clk), .Q(D1), .clr(R));
  Register VR2 (.D(Data), .en(R2), .clk(Clk), .Q(D2), .clr(R));
  Register VR3 (.D(Data), .en(R3), .clk(Clk), .Q(D3), .clr(R));
  Multiplexer #(.select(2), .width(8)) multiplexer_1 (
    .in0({8{1'b0}}), .in1(D1), .in2(D2), .in3(D3), .out(RD1), .sel(RA));
  Multiplexer #(.select(2), .width(8)) multiplexer_2 (
    .in0({8{1'b0}}), .in1(D1), .in2(D2), .in3(D3), .out(RD2), .sel(RB));

  // Notes on the sheet:
  //   VR0
endmodule

module VPE1_Register_Bank (
  input  [7:0] Data,
  input  [1:0] RA,
  input  WE,
  input  [1:0] RD,
  input  [1:0] RB,
  input  Clk,
  input  R,
  output [7:0] RD1,
  output [7:0] RD2
);

  wire demultiplexer_1_out0, R1, R2, R3;
  wire [7:0] D1, D2, D3;

  // NoConnect on demultiplexer_1_out0
  Demultiplexer #(.select(2)) demultiplexer_1 (
    .out0(demultiplexer_1_out0), .out1(R1), .out2(R2), .out3(R3), .in(WE), .sel(RD));
  Register VR1 (.D(Data), .en(R1), .clk(Clk), .Q(D1), .clr(R));
  Register VR2 (.D(Data), .en(R2), .clk(Clk), .Q(D2), .clr(R));
  Register VR3 (.D(Data), .en(R3), .clk(Clk), .Q(D3), .clr(R));
  Multiplexer #(.select(2), .width(8)) multiplexer_1 (.in0(8'h1), .in1(D1), .in2(D2), .in3(D3), .out(RD1), .sel(RA));
  Multiplexer #(.select(2), .width(8)) multiplexer_2 (.in0(8'h1), .in1(D1), .in2(D2), .in3(D3), .out(RD2), .sel(RB));

  // Notes on the sheet:
  //   VR0
endmodule

module VPE2_Register_Bank (
  input  [7:0] Data,
  input  [1:0] RA,
  input  WE,
  input  [1:0] RD,
  input  [1:0] RB,
  input  Clk,
  input  R,
  output [7:0] RD1,
  output [7:0] RD2
);

  wire demultiplexer_1_out0, R1, R2, R3;
  wire [7:0] D1, D2, D3;

  // NoConnect on demultiplexer_1_out0
  Demultiplexer #(.select(2)) demultiplexer_1 (
    .out0(demultiplexer_1_out0), .out1(R1), .out2(R2), .out3(R3), .in(WE), .sel(RD));
  Register VR1 (.D(Data), .en(R1), .clk(Clk), .Q(D1), .clr(R));
  Register VR2 (.D(Data), .en(R2), .clk(Clk), .Q(D2), .clr(R));
  Register VR3 (.D(Data), .en(R3), .clk(Clk), .Q(D3), .clr(R));
  Multiplexer #(.select(2), .width(8)) multiplexer_1 (.in0(8'h2), .in1(D1), .in2(D2), .in3(D3), .out(RD1), .sel(RA));
  Multiplexer #(.select(2), .width(8)) multiplexer_2 (.in0(8'h2), .in1(D1), .in2(D2), .in3(D3), .out(RD2), .sel(RB));

  // Notes on the sheet:
  //   VR0
endmodule

module VPE3_Register_Bank (
  input  [7:0] Data,
  input  [1:0] RA,
  input  WE,
  input  [1:0] RD,
  input  [1:0] RB,
  input  Clk,
  input  R,
  output [7:0] RD1,
  output [7:0] RD2
);

  wire demultiplexer_1_out0, R1, R2, R3;
  wire [7:0] D1, D2, D3;

  // NoConnect on demultiplexer_1_out0
  Demultiplexer #(.select(2)) demultiplexer_1 (
    .out0(demultiplexer_1_out0), .out1(R1), .out2(R2), .out3(R3), .in(WE), .sel(RD));
  Register VR1 (.D(Data), .en(R1), .clk(Clk), .Q(D1), .clr(R));
  Register VR2 (.D(Data), .en(R2), .clk(Clk), .Q(D2), .clr(R));
  Register VR3 (.D(Data), .en(R3), .clk(Clk), .Q(D3), .clr(R));
  Multiplexer #(.select(2), .width(8)) multiplexer_1 (.in0(8'h3), .in1(D1), .in2(D2), .in3(D3), .out(RD1), .sel(RA));
  Multiplexer #(.select(2), .width(8)) multiplexer_2 (.in0(8'h3), .in1(D1), .in2(D2), .in3(D3), .out(RD2), .sel(RB));

  // Notes on the sheet:
  //   VR0
endmodule

module VPE_ULA (
  input  [7:0] RA,
  input  [7:0] RB,
  input  [2:0] ULA_Op,
  output [7:0] out_4
);

  wire comparator_1_eq;
  wire [7:0] R2, R3, R4;

  // NoConnect on RA[7:4]
  // NoConnect on RB[7:4]
  // NoConnect on RB[7:4]
  // NoConnect on RA[3:0]
  Adder adder_1 (.a(RA), .b(RB), .out(R2));  // open: cin, cout
  Subtractor subtractor_1 (.a(RA), .b(RB), .out(R3));  // open: bin, bout
  assign R4 = {{7{comparator_1_eq}}, comparator_1_eq};  // Bit_Extender bit_extender_1
  Comparator comparator_1 (.a(RA), .b(RB), .eq(comparator_1_eq));  // open: gt, lt
  Multiplexer #(.select(3), .width(8)) multiplexer_1 (
    .in0({RB[3:0], RA[3:0]}), .in1({RA[7:4], RB[3:0]}), .in2(R2), .in3(R3), .in4(R4), .in5({8{1'b0}}),
    .in6({8{1'b0}}), .in7({8{1'b0}}), .out(out_4), .sel(ULA_Op));

  // Other names for the same wires on the sheet: R0[7:0] = {RB[3:0], RA[3:0]}; R1[7:0] = {RA[7:4], RB[3:0]}

  // Notes on the sheet:
  //   Move High
  //   Move Low
  //   Adder
  //   Subtractor
  //   Comparator
endmodule

module VPE_Memory_Data (
  input  [7:0] Addr,
  input  WM,
  input  Clk,
  input  [7:0] d,
  output [7:0] data
);

  RAM #(.trigger("falling")) ram_1 (.addr(Addr), .we(WM), .oe(1'b1), .clk(Clk), .din(d), .dout(data));
endmodule

module Stg_IF_ID (
  input  [7:0] Inst_IF,
  input  Clk,
  input  R,
  output [7:0] Inst_ID
);

  wire [7:0] register_1_q, undriven;

  Register register_1 (.D(undriven), .en(1'b1), .clk(Clk), .Q(register_1_q), .clr(R));
  Register register_2 (.D(Inst_IF), .en(1'b1), .clk(Clk), .Q(Inst_ID), .clr(R));
endmodule

module Stg_ID_EX_Spe (
  input  [4:0] ExeSgn_Id,
  input  [1:0] MemSgn_Id,
  input  WbSgn_Id,
  input  [7:0] RD1_Id,
  input  [7:0] RD2_Id,
  input  [5:0] ARs_Id,
  input  [7:0] Imm_Id,
  input  Clk,
  input  R,
  output [4:0] ExeSgn_Exe,
  output [1:0] MemSgn_Exe,
  output WbSgn_Exe,
  output [7:0] RD1_Exe,
  output [7:0] RD2_Exe,
  output [5:0] ARs_Exe,
  output [7:0] Imm_Exe
);

  wire undriven;

  Register #(.width(5)) EXE (.D(ExeSgn_Id), .en(1'b1), .clk(Clk), .Q(ExeSgn_Exe), .clr(undriven));
  Register #(.width(2)) MEM (.D(MemSgn_Id), .en(1'b1), .clk(Clk), .Q(MemSgn_Exe), .clr(undriven));
  Register #(.width(1)) WB (.D(WbSgn_Id), .en(1'b1), .clk(Clk), .Q(WbSgn_Exe), .clr(undriven));
  Register RD1 (.D(RD1_Id), .en(1'b1), .clk(Clk), .Q(RD1_Exe), .clr(undriven));
  Register RD2 (.D(RD2_Id), .en(1'b1), .clk(Clk), .Q(RD2_Exe), .clr(undriven));
  Register #(.width(6)) AdRs (.D(ARs_Id), .Q(ARs_Exe), .clr(undriven));  // open: en, clk
  Register Imm (.D(Imm_Id), .en(1'b1), .clk(Clk), .Q(Imm_Exe), .clr(R));
endmodule

module Stg_EX_MEM_Spe (
  input  [1:0] MemSgn_Exe,
  input  WbSgn_Exe,
  input  [7:0] UlaR_Exe,
  input  [7:0] Addr_Exe,
  input  [1:0] Data_Exe,
  input  [7:0] AddrR_Exe,
  input  Clk,
  input  R,
  output [1:0] MemSgn_Mem,
  output WbSgn_Mem,
  output [7:0] UlaR_Mem,
  output [7:0] Addr_Mem,
  output [1:0] Data_Mem,
  output [7:0] AddrR_Mem
);

  wire undriven;

  Register #(.width(2)) MEM (.D(MemSgn_Exe), .en(1'b1), .clk(Clk), .Q(MemSgn_Mem), .clr(undriven));
  Register #(.width(1)) WB (.D(WbSgn_Exe), .en(1'b1), .clk(Clk), .Q(WbSgn_Mem), .clr(undriven));
  Register UlaR (.D(UlaR_Exe), .en(1'b1), .clk(Clk), .Q(UlaR_Mem), .clr(undriven));
  Register Addr (.D(Addr_Exe), .en(1'b1), .clk(Clk), .Q(Addr_Mem), .clr(undriven));
  Register #(.width(2)) Data (.D(Data_Exe), .en(1'b1), .clk(Clk), .Q(Data_Mem), .clr(undriven));
  Register AddrR (.D(AddrR_Exe), .en(1'b1), .clk(Clk), .Q(AddrR_Mem), .clr(R));
endmodule

module Stg_MEM_WB_Spe (
  input  WbSgn_Exe,
  input  [1:0] Data_Exe,
  input  [7:0] AddrR_Exe,
  input  Clk,
  input  R,
  output WbSgn_Mem,
  output [1:0] Data_Mem,
  output [7:0] AddrR_Mem
);

  wire undriven;

  Register #(.width(1)) WB (.D(WbSgn_Exe), .en(1'b1), .clk(Clk), .Q(WbSgn_Mem), .clr(undriven));
  Register #(.width(2)) Data (.D(Data_Exe), .en(1'b1), .clk(Clk), .Q(Data_Mem), .clr(undriven));
  Register AddrR (.D(AddrR_Exe), .en(1'b1), .clk(Clk), .Q(AddrR_Mem), .clr(R));
endmodule
