// Logisim project Sagui_VetorialP.circ as structural Verilog: 29 circuits, main circuit main
module main (
);

  wire Br, Clk, comparator_1_eq, Eb, En, hnop, IsBr, MD, MEb, multiplexer_17_out, or_1_out, or_2_out,
       or_5_out, or_6_out, R, R_Str, S_USr, S_WE, V_MD, V_MSti, V_USr, V_WE, V_WM, Vec, W, WBS, WBS_Ex,
       WBS_Me, xor_1_out, xor_2_out;
  wire [1:0] FA, FB, FBr, MemS, MemS_Ex, multiplexer_14_out, multiplexer_16_out, or_3_out, or_4_out, RA,
       RA_Ex, RA_ID, RB_Ex, RB_ID, RD_Ex, RD_Me, RD_WB, V_Id, V_Mem, V_WB, VFA, VFB, VMemEx, VMemId, VRA_EX,
       VRA_ID, VRB_EX, VRD_EX, VRD_ME, VRD_WB, VWbEx, VWbId, VWbMe;
  wire [2:0] S_UOp, V_UOp;
  wire [2:2] ID;
  wire [3:0] ExeS, multiplexer_15_out, Opcode, V_Exe, VExeId;
  wire [7:0] adder_1_out, Addr, Addr0, Addr1, Addr2, Addr3, AddrEx, AE0, AE1, AE2, AE3, d, d0, d1, d2, d3,
       Data0, Data1, Data2, Data3, DE0, DE1, DE2, DE3, DtEx, imm, imm_EX, imm_ex_t,
       memory_instruction_1_inst, multiplexer_1_out, multiplexer_2_out, multiplexer_3_out, multiplexer_7_out,
       multiplexer_8_out, multiplexer_9_out, multiplexer_10_out, multiplexer_11_out, multiplexer_28_out,
       multiplexer_29_out, multiplexer_30_out, multiplexer_31_out, multiplexer_32_out, multiplexer_33_out,
       multiplexer_34_out, multiplexer_35_out, multiplexer_36_out, multiplexer_37_out, NPtr0Me, NPtr0Wb,
       NPtr1Me, NPtr1Wb, NPtr2Me, NPtr2Wb, NPtr3Me, NPtr3Wb, PCA, program_counter_1_pc_n, RUla, S_Data,
       spe_memory_data_1_data, spe_register_bank_1_rd1, spe_register_bank_1_rd2, stg_id_ex_spe_1_rd1_exe,
       stg_id_ex_spe_1_rd2_exe, stg_id_ex_vpe_1_rd1_exe, stg_id_ex_vpe_1_rd2_exe, stg_id_ex_vpe_2_rd1_exe,
       stg_id_ex_vpe_2_rd2_exe, stg_id_ex_vpe_3_rd1_exe, stg_id_ex_vpe_3_rd2_exe, stg_id_ex_vpe_4_rd1_exe,
       stg_id_ex_vpe_4_rd2_exe, V_UR0, V_UR1, V_UR2, V_UR3, vpe0_register_bank_1_rd1,
       vpe0_register_bank_1_rd2, vpe1_register_bank_1_rd1, vpe1_register_bank_1_rd2,
       vpe2_register_bank_1_rd1, vpe2_register_bank_1_rd2, vpe3_register_bank_1_rd1,
       vpe3_register_bank_1_rd2, vpe_memory_data_1_data, vpe_memory_data_2_data, vpe_memory_data_3_data,
       vpe_memory_data_4_data, vpe_ula_1_out_4, vpe_ula_2_out_4, vpe_ula_3_out_4, vpe_ula_4_out_4;
  wire [9:0] VS;

  Multiplexer #(.width(8)) multiplexer_1 (.in0(adder_1_out), .in1(PCA), .out(multiplexer_1_out), .sel(xor_1_out));
  xor xor_1 (xor_1_out, IsBr, MEb);
  Program_Counter program_counter_1 (
    .PC_P(multiplexer_1_out), .En(xor_2_out), .Clk(Clk), .R(R), .PC_N(program_counter_1_pc_n));
  xor xor_2 (xor_2_out, R_Str, En);
  Multiplexer #(.width(8)) multiplexer_2 (.in0(8'h1), .in1({8{1'b1}}), .out(multiplexer_2_out), .sel(MEb));
  Adder adder_1 (.a(program_counter_1_pc_n), .b(multiplexer_2_out), .out(adder_1_out));  // open: cin, cout
  Clock clock_1 (.out(Clk));
  Button Reset (.out(R));
  Memory_Instruction memory_instruction_1 (.Addr_PC(program_counter_1_pc_n), .Inst(memory_instruction_1_inst));
  Start_Reset start_reset_1 (.clk(Clk), .R(R), .R_Start(R_Str));
  Multiplexer #(.width(8)) multiplexer_3 (
    .in0(memory_instruction_1_inst), .in1(8'h40), .out(multiplexer_3_out), .sel(or_1_out));
  or or_1 (or_1_out, hnop, R_Str);
  Stg_IF_ID stg_if_id_1 (.Inst_IF(multiplexer_3_out), .En(En), .Clk(Clk), .R(R), .Inst_ID({Opcode, RA, RB_ID}));
  or or_2 (or_2_out, MemS_Ex[0], VMemEx[1]);
  assign or_3_out = RA_ID | VRA_ID;  // OR_Gate or_3, 2 bits wide
  Multiplexer #(.width(2)) multiplexer_4 (.in0(RA), .in1(2'b01), .out(VRA_ID), .sel(V_Id[1]));
  assign or_4_out = RD_Ex | VRD_EX;  // OR_Gate or_4, 2 bits wide
  Multiplexer #(.width(2)) multiplexer_5 (.in0(RA), .in1(2'b01), .out(RA_ID), .sel(ID[2]));
  VPE_Ctrl vpe_ctrl_1 (.VectorSigns(VS), .ID_V(V_Id), .EXE_V(V_Exe), .MEM_V(V_Mem), .WB_V(V_WB));
  Hazard_Unit hazard_unit_1 (
    .RD_ex(or_4_out), .RB_id(RB_ID), .RA_id(or_3_out), .MemRead(or_2_out), .Br(IsBr), .hnop(hnop), .EN(En));
  or or_5 (or_5_out, hnop, ~Vec);  // OR_Gate
  Multiplexer #(.width(4)) multiplexer_6 (.in0(V_Exe), .in1(4'b0000), .out(VExeId), .sel(or_5_out));
  assign imm = {{4{RA[1]}}, {RA, RB_ID}};  // Bit_Extender bit_extender_1
  Control_Unit control_unit_1 (
    .Opcode(Opcode), .Vec(Vec), .RadSpe(ID[2]), .BrSpe(Br), .Ebreak(Eb), .UlaOpSpe(ExeS[3:1]),
    .UlaSrSpe(ExeS[0]), .MDSpe(MemS[1]), .WMSpe(MemS[0]), .WESpe(WBS), .VecSg(VS));
  SPE_Register_Bank spe_register_bank_1 (
    .WE(S_WE), .Data(S_Data), .RD(RD_WB), .Clk(Clk), .R(R), .RA(RA_ID), .RB(RB_ID),
    .RD1(spe_register_bank_1_rd1), .RD2(spe_register_bank_1_rd2));
  Multiplexer #(.width(8)) multiplexer_7 (.in0(d0), .in1(NPtr0Wb), .out(multiplexer_7_out), .sel(V_MSti));
  Multiplexer #(.width(8)) multiplexer_8 (.in0(d1), .in1(NPtr1Wb), .out(multiplexer_8_out), .sel(V_MSti));
  Multiplexer #(.width(8)) multiplexer_9 (.in0(d2), .in1(NPtr2Wb), .out(multiplexer_9_out), .sel(V_MSti));
  Multiplexer #(.width(8)) multiplexer_10 (.in0(d3), .in1(NPtr3Wb), .out(multiplexer_10_out), .sel(V_MSti));
  Multiplexer #(.select(2), .width(8)) multiplexer_11 (
    .in0(spe_register_bank_1_rd1), .in1(RUla), .in2(PCA), .in3({8{1'b0}}), .out(multiplexer_11_out), .sel(FBr));
  Multiplexer #(.width(2)) multiplexer_12 (.in0(V_Mem), .in1(2'b00), .out(VMemId), .sel(or_5_out));
  Multiplexer #(.width(2)) multiplexer_13 (.in0(V_WB), .in1(2'b00), .out(VWbId), .sel(or_5_out));
  Ebreak ebreak_1 (.RA(RA), .RB(RB_ID), .Eb(Eb), .MEb(MEb));
  Comparator comparator_1 (.a(multiplexer_11_out), .b({8{1'b0}}), .eq(comparator_1_eq));  // open: gt, lt
  ForwardingBranch_Unit forwardingbranch_unit_1 (
    .Rd_ExMem(RD_Me), .Rd_IdEx(RD_Ex), .Ra_id(RA_ID), .WE_IdEx(WBS_Ex), .WE_ExMem(WBS_Me), .Forw_Br(FBr));
  Multiplexer #(.width(2)) multiplexer_14 (.in0(VRA_ID), .in1(RB_ID), .out(multiplexer_14_out), .sel(V_Id[0]));
  and and_1 (IsBr, Br, comparator_1_eq);
  VPE0_Register_Bank vpe0_register_bank_1 (
    .WE(V_WE), .Data(multiplexer_7_out), .RD(VRD_WB), .Clk(Clk), .R(R), .RA(VRA_ID), .RB(RB_ID),
    .RD1(vpe0_register_bank_1_rd1), .RD2(vpe0_register_bank_1_rd2));
  VPE1_Register_Bank vpe1_register_bank_1 (
    .WE(V_WE), .Data(multiplexer_8_out), .RD(VRD_WB), .Clk(Clk), .R(R), .RA(VRA_ID), .RB(RB_ID),
    .RD1(vpe1_register_bank_1_rd1), .RD2(vpe1_register_bank_1_rd2));
  VPE2_Register_Bank vpe2_register_bank_1 (
    .WE(V_WE), .Data(multiplexer_9_out), .RD(VRD_WB), .Clk(Clk), .R(R), .RA(VRA_ID), .RB(RB_ID),
    .RD1(vpe2_register_bank_1_rd1), .RD2(vpe2_register_bank_1_rd2));
  VPE3_Register_Bank vpe3_register_bank_1 (
    .WE(V_WE), .Data(multiplexer_10_out), .RD(VRD_WB), .Clk(Clk), .R(R), .RA(VRA_ID), .RB(RB_ID),
    .RD1(vpe3_register_bank_1_rd1), .RD2(vpe3_register_bank_1_rd2));
  or or_6 (or_6_out, Vec, hnop);
  Multiplexer #(.width(4)) multiplexer_15 (.in0(ExeS), .in1(4'b0000), .out(multiplexer_15_out), .sel(or_6_out));
  Multiplexer #(.width(2)) multiplexer_16 (.in0(MemS), .in1(2'b00), .out(multiplexer_16_out), .sel(or_6_out));
  Multiplexer multiplexer_17 (.in0(WBS), .in1(1'b0), .out(multiplexer_17_out), .sel(or_6_out));
  Stg_ID_EX_Vpe_General stg_id_ex_vpe_general_1 (
    .ExeSgn_Id(VExeId), .MemSgn_Id(VMemId), .WbSgn_Id(VWbId), .ARs_Id({multiplexer_14_out, RB_ID, VRA_ID}),
    .Imm_Id(imm), .Clk(Clk), .R(R), .ExeSgn_Exe({V_USr, V_UOp}), .MemSgn_Exe(VMemEx), .WbSgn_Exe(VWbEx),
    .Imm_Exe(imm_EX), .ARs_Exe({VRD_EX, VRB_EX, VRA_EX}));
  Stg_ID_EX_Vpe stg_id_ex_vpe_1 (
    .RD1_Id(vpe0_register_bank_1_rd1), .RD2_Id(vpe0_register_bank_1_rd2), .Clk(Clk), .R(R),
    .RD1_Exe(stg_id_ex_vpe_1_rd1_exe), .RD2_Exe(stg_id_ex_vpe_1_rd2_exe));
  Stg_ID_EX_Vpe stg_id_ex_vpe_2 (
    .RD1_Id(vpe1_register_bank_1_rd1), .RD2_Id(vpe1_register_bank_1_rd2), .Clk(Clk), .R(R),
    .RD1_Exe(stg_id_ex_vpe_2_rd1_exe), .RD2_Exe(stg_id_ex_vpe_2_rd2_exe));
  Stg_ID_EX_Vpe stg_id_ex_vpe_3 (
    .RD1_Id(vpe2_register_bank_1_rd1), .RD2_Id(vpe2_register_bank_1_rd2), .Clk(Clk), .R(R),
    .RD1_Exe(stg_id_ex_vpe_3_rd1_exe), .RD2_Exe(stg_id_ex_vpe_3_rd2_exe));
  Stg_ID_EX_Vpe stg_id_ex_vpe_4 (
    .RD1_Id(vpe3_register_bank_1_rd1), .RD2_Id(vpe3_register_bank_1_rd2), .Clk(Clk), .R(R),
    .RD1_Exe(stg_id_ex_vpe_4_rd1_exe), .RD2_Exe(stg_id_ex_vpe_4_rd2_exe));
  Stg_ID_EX_Spe stg_id_ex_spe_1 (
    .Imm_Id(imm), .ExeSgn_Id(multiplexer_15_out), .MemSgn_Id(multiplexer_16_out),
    .WbSgn_Id(multiplexer_17_out), .RD1_Id(spe_register_bank_1_rd1), .RD2_Id(spe_register_bank_1_rd2),
    .ARs_Id({RA_ID, RB_ID, RA_ID}), .Clk(Clk), .R(R), .Imm_Exe(imm_ex_t), .ExeSgn_Exe({S_UOp, S_USr}),
    .MemSgn_Exe(MemS_Ex), .WbSgn_Exe(WBS_Ex), .RD1_Exe(stg_id_ex_spe_1_rd1_exe),
    .RD2_Exe(stg_id_ex_spe_1_rd2_exe), .ARs_Exe({RD_Ex, RB_Ex, RA_Ex}));
  Multiplexer #(.select(2), .width(8)) multiplexer_18 (
    .in0(stg_id_ex_vpe_1_rd1_exe), .in1(d0), .in2(V_UR0), .in3({8{1'b0}}), .out(DE0), .sel(VFA));
  Multiplexer #(.select(2), .width(8)) multiplexer_19 (
    .in0(stg_id_ex_vpe_1_rd2_exe), .in1(d0), .in2(V_UR0), .in3({8{1'b0}}), .out(AE0), .sel(VFB));
  Multiplexer #(.select(2), .width(8)) multiplexer_20 (
    .in0(stg_id_ex_vpe_2_rd1_exe), .in1(d1), .in2(V_UR1), .in3({8{1'b0}}), .out(DE1), .sel(VFA));
  Multiplexer #(.select(2), .width(8)) multiplexer_21 (
    .in0(stg_id_ex_vpe_2_rd2_exe), .in1(d1), .in2(V_UR1), .in3({8{1'b0}}), .out(AE1), .sel(VFB));
  Multiplexer #(.select(2), .width(8)) multiplexer_22 (
    .in0(stg_id_ex_vpe_3_rd1_exe), .in1(d2), .in2(V_UR2), .in3({8{1'b0}}), .out(DE2), .sel(VFA));
  Multiplexer #(.select(2), .width(8)) multiplexer_23 (
    .in0(stg_id_ex_vpe_3_rd2_exe), .in1(d2), .in2(V_UR2), .in3({8{1'b0}}), .out(AE2), .sel(VFB));
  Multiplexer #(.select(2), .width(8)) multiplexer_24 (
    .in0(stg_id_ex_vpe_4_rd1_exe), .in1(d3), .in2(V_UR3), .in3({8{1'b0}}), .out(DE3), .sel(VFA));
  Multiplexer #(.select(2), .width(8)) multiplexer_25 (
    .in0(stg_id_ex_vpe_4_rd2_exe), .in1(d3), .in2(V_UR3), .in3({8{1'b0}}), .out(AE3), .sel(VFB));
  Multiplexer #(.select(2), .width(8)) multiplexer_26 (
    .in0(stg_id_ex_spe_1_rd1_exe), .in1(S_Data), .in2(RUla), .in3({8{1'b0}}), .out(DtEx), .sel(FA));
  Multiplexer #(.select(2), .width(8)) multiplexer_27 (
    .in0(stg_id_ex_spe_1_rd2_exe), .in1(S_Data), .in2(RUla), .in3({8{1'b0}}), .out(AddrEx));  // open: sel
  Multiplexer #(.width(8)) multiplexer_28 (.in0(AE0), .in1(imm_EX), .out(multiplexer_28_out), .sel(V_USr));
  Multiplexer #(.width(8)) multiplexer_29 (.in0(AE1), .in1(imm_EX), .out(multiplexer_29_out), .sel(V_USr));
  Multiplexer #(.width(8)) multiplexer_30 (.in0(AE2), .in1(imm_EX), .out(multiplexer_30_out), .sel(V_USr));
  Multiplexer #(.width(8)) multiplexer_31 (.in0(AE3), .in1(imm_EX), .out(multiplexer_31_out), .sel(V_USr));
  Multiplexer #(.width(8)) multiplexer_32 (.in0(AddrEx), .in1(imm_ex_t), .out(multiplexer_32_out), .sel(S_USr));
  ForwardingULA_Unit forwardingula_unit_1 (
    .Rd_MemWb(VRD_WB), .Rd_ExMem(VRD_ME), .Rb(VRB_EX), .Ra(VRA_EX), .WE_ExMem(VWbMe[0]), .WE_MemWb(V_WE),
    .Forw_A(VFA), .Forw_B(VFB));
  VPE_ULA vpe_ula_1 (.ULA_Op(V_UOp), .RA(DE0), .RB(multiplexer_28_out), .out_4(vpe_ula_1_out_4));
  VPE_ULA vpe_ula_2 (.ULA_Op(V_UOp), .RA(DE1), .RB(multiplexer_29_out), .out_4(vpe_ula_2_out_4));
  VPE_ULA vpe_ula_3 (.ULA_Op(V_UOp), .RA(DE2), .RB(multiplexer_30_out), .out_4(vpe_ula_3_out_4));
  VPE_ULA vpe_ula_4 (.ULA_Op(V_UOp), .RA(DE3), .RB(multiplexer_31_out), .out_4(vpe_ula_4_out_4));
  SPE_ULA spe_ula_1 (.ULA_Op(S_UOp), .RA(DtEx), .RB(multiplexer_32_out), .out_4(PCA));
  ForwardingULA_Unit forwardingula_unit_2 (
    .Rd_MemWb(RD_WB), .Rd_ExMem(RD_Me), .Rb(RB_Ex), .Ra(RA_Ex), .WE_ExMem(WBS_Me), .WE_MemWb(S_WE),
    .Forw_A(FA), .Forw_B(FB));
  Stg_EX_MEM_VPE_General stg_ex_mem_vpe_general_1 (
    .AddrR_Exe(VRD_EX), .MemSgn_Exe(VMemEx), .WbSgn_Exe(VWbEx), .Clk(Clk), .R(R), .AddrR_Mem(VRD_ME),
    .MemSgn_Mem({V_MD, V_WM}), .WbSgn_Mem(VWbMe));
  Stg_EX_MEM_Vpe stg_ex_mem_vpe_1 (
    .UlaR_Exe(vpe_ula_1_out_4), .Addr_Exe(AE0), .Data_Exe(DE0), .Clk(Clk), .R(R), .UlaR_Mem(V_UR0),
    .Addr_Mem(Addr0), .Data_Mem(Data0));
  Stg_EX_MEM_Vpe stg_ex_mem_vpe_2 (
    .UlaR_Exe(vpe_ula_2_out_4), .Addr_Exe(AE1), .Data_Exe(DE1), .Clk(Clk), .R(R), .UlaR_Mem(V_UR1),
    .Addr_Mem(Addr1), .Data_Mem(Data1));
  Stg_EX_MEM_Vpe stg_ex_mem_vpe_3 (
    .UlaR_Exe(vpe_ula_3_out_4), .Addr_Exe(AE2), .Data_Exe(DE2), .Clk(Clk), .R(R), .UlaR_Mem(V_UR2),
    .Addr_Mem(Addr2), .Data_Mem(Data2));
  Stg_EX_MEM_Vpe stg_ex_mem_vpe_4 (
    .UlaR_Exe(vpe_ula_4_out_4), .Addr_Exe(AE3), .Data_Exe(DE3), .Clk(Clk), .R(R), .UlaR_Mem(V_UR3),
    .Addr_Mem(Addr3), .Data_Mem(Data3));
  Stg_EX_MEM_Spe stg_ex_mem_spe_1 (
    .AddrR_Exe(RD_Ex), .MemSgn_Exe(MemS_Ex), .WbSgn_Exe(WBS_Ex), .UlaR_Exe(PCA), .Addr_Exe(AddrEx),
    .Data_Exe(DtEx), .Clk(Clk), .R(R), .AddrR_Mem(RD_Me), .MemSgn_Mem({W, MD}), .WbSgn_Mem(WBS_Me),
    .UlaR_Mem(RUla), .Addr_Mem(Addr), .Data_Mem(d));
  Adder adder_2 (.a(8'h4), .b(Addr0), .out(NPtr0Me));  // open: cin, cout
  Adder adder_3 (.a(8'h4), .b(Addr1), .out(NPtr1Me));  // open: cin, cout
  Adder adder_4 (.a(8'h4), .b(Addr2), .out(NPtr2Me));  // open: cin, cout
  Adder adder_5 (.a(8'h4), .b(Addr3), .out(NPtr3Me));  // open: cin, cout
  VPE_Memory_Data vpe_memory_data_1 (.Addr(Addr0), .WM(V_WM), .Clk(Clk), .d(Data0), .data(vpe_memory_data_1_data));
  VPE_Memory_Data vpe_memory_data_2 (.Addr(Addr1), .WM(V_WM), .Clk(Clk), .d(Data1), .data(vpe_memory_data_2_data));
  VPE_Memory_Data vpe_memory_data_3 (.Addr(Addr2), .WM(V_WM), .Clk(Clk), .d(Data2), .data(vpe_memory_data_3_data));
  VPE_Memory_Data vpe_memory_data_4 (.Addr(Addr3), .WM(V_WM), .Clk(Clk), .d(Data3), .data(vpe_memory_data_4_data));
  SPE_Memory_Data spe_memory_data_1 (.Addr(Addr), .WM(W), .Clk(Clk), .d(d), .data(spe_memory_data_1_data));
  Multiplexer #(.width(8)) multiplexer_33 (
    .in0(V_UR0), .in1(vpe_memory_data_1_data), .out(multiplexer_33_out), .sel(V_MD));
  Multiplexer #(.width(8)) multiplexer_34 (
    .in0(V_UR1), .in1(vpe_memory_data_2_data), .out(multiplexer_34_out), .sel(V_MD));
  Multiplexer #(.width(8)) multiplexer_35 (
    .in0(V_UR2), .in1(vpe_memory_data_3_data), .out(multiplexer_35_out), .sel(V_MD));
  Multiplexer #(.width(8)) multiplexer_36 (
    .in0(V_UR3), .in1(vpe_memory_data_4_data), .out(multiplexer_36_out), .sel(V_MD));
  Multiplexer #(.width(8)) multiplexer_37 (
    .in0(RUla), .in1(spe_memory_data_1_data), .out(multiplexer_37_out), .sel(MD));
  Stg_MEM_WB_Vpe_General stg_mem_wb_vpe_general_1 (
    .WbSgn_Mem(VWbMe), .AddrR_Mem(VRD_ME), .Clk(Clk), .R(R), .WbSgn_WB({V_MSti, V_WE}), .AddrR_WB(VRD_WB));
  Stg_MEM_WB_Vpe stg_mem_wb_vpe_1 (
    .Data_Mem(multiplexer_33_out), .NPtr_Mem(NPtr0Me), .Clk(Clk), .R(R), .Data_WB(d0), .NPtr_WB(NPtr0Wb));
  Stg_MEM_WB_Vpe stg_mem_wb_vpe_2 (
    .Data_Mem(multiplexer_34_out), .NPtr_Mem(NPtr1Me), .Clk(Clk), .R(R), .Data_WB(d1), .NPtr_WB(NPtr1Wb));
  Stg_MEM_WB_Vpe stg_mem_wb_vpe_3 (
    .Data_Mem(multiplexer_35_out), .NPtr_Mem(NPtr2Me), .Clk(Clk), .R(R), .Data_WB(d2), .NPtr_WB(NPtr2Wb));
  Stg_MEM_WB_Vpe stg_mem_wb_vpe_4 (
    .Data_Mem(multiplexer_36_out), .NPtr_Mem(NPtr3Me), .Clk(Clk), .R(R), .Data_WB(d3), .NPtr_WB(NPtr3Wb));
  Stg_MEM_WB_Spe stg_mem_wb_spe_1 (
    .AddrR_Mem(RD_Me), .WbSgn_Mem(WBS_Me), .Data_Mem(multiplexer_37_out), .Clk(Clk), .R(R), .AddrR_WB(RD_WB),
    .WbSgn_WB(S_WE), .Data_WB(S_Data));

  // Other names for the same wires on the sheet: RD_ID[1:0] = RA_ID; ID[1:0] = {Br, Eb}; RAD = ID[2];
  //   RiUla[7:0] = PCA; V_MRd = V_Id[0]; V_RAD = V_Id[1]; VWeMe = VWbMe[0]

  // Notes on the sheet:
  //   RA's addr
  //   VPE: control signs
  //   VPE: Register bank's control signs
  //   VPE: ALU's control signs
  //   VPE: Memory's control signs
  //   VPE: Write back's control signs
  //   =============================================== Vector Processing Element ===============================================
  //   ========================================================= VPE0 =========================================================
  //   ========================================================= VPE1 =========================================================
  //   ========================================================= VPE2 =========================================================
  //   ========================================================= VPE3 =========================================================
  //   =============================================== Scalar Processing Element ===============================================
  //   Vectorial Forwading 
  //   Next address
  //   Next address
  //   Next address
  //   Next address
endmodule

module Program_Counter (
  input  [7:0] PC_P,
  input  En,
  input  Clk,
  input  R,
  output [7:0] PC_N
);

  Register PC (.D(PC_P), .en(En), .clk(Clk), .Q(PC_N), .clr(R));
endmodule

module Memory_Instruction (
  input  [7:0] Addr_PC,
  output [7:0] Inst
);

  ROM rom_1 (.addr(Addr_PC), .data(Inst));

  // Notes on the sheet:
  //   contents of rom_1 (hex, n*v repeats v):
  //   c8 cc b4 32 49 ee 3d 79 cd 31 59 35 71 32 49 bc cd b4 ee 21 3d 79 cd 20 31 59 21 32 71 55 32 49 b0
  //   e6 22 3b 79 20 31 59 22 31 71 55 32 49 da c8 8e a0 bc c9 86 cd a0 bc c9 9e 24 36 79 20 31 59 a1 b4
  //   d9 23 30 71 70
endmodule

module Control_Unit (
  input  [3:0] Opcode,
  output Vec,
  output RadSpe,
  output BrSpe,
  output Ebreak,
  output [2:0] UlaOpSpe,
  output UlaSrSpe,
  output MDSpe,
  output WMSpe,
  output WESpe,
  output [9:0] VecSg
);

  ROM #(.addrWidth(4), .dataWidth(21)) rom_1 (
    .addr(Opcode), .data({Vec, RadSpe, BrSpe, Ebreak, UlaOpSpe, UlaSrSpe, MDSpe, WMSpe, WESpe, VecSg}));

  // Notes on the sheet:
  //   contents of rom_1 (hex, n*v repeats v):
  //   1400 800 82400 86400 8400 c400 10400 60000 100009 100004 100281 100291 100021 100031 100107 100041
  //   Total de bits: 21
  //   0..9: signs of the vector part
  //   10..20: signs of the scalar part
  //   21: control bit between scalar and vector instructions
endmodule

module Ebreak (
  input  [1:0] RA,
  input  Eb,
  input  [1:0] RB,
  output MEb
);

  wire comparator_1_eq, comparator_2_eq;

  Comparator #(.width(2)) comparator_1 (.a(RA), .b(2'b00), .eq(comparator_1_eq));  // open: gt, lt
  Comparator #(.width(2)) comparator_2 (.a(RB), .b(2'b00), .eq(comparator_2_eq));  // open: gt, lt
  and and_1 (MEb, comparator_1_eq, Eb, comparator_2_eq);
endmodule

module Start_Reset (
  input  R,
  input  clk,
  output R_Start
);

  wire d_ff_1_qn;

  D_Flip_Flop d_ff_1 (.clk(clk), .Q(R_Start), .Qn(d_ff_1_qn), .preset(R), .reset(clk));  // open: D
  // NoConnect on d_ff_1_qn
endmodule

module SPE_Register_Bank (
  input  [7:0] Data,
  input  [1:0] RA,
  input  WE,
  input  [1:0] RD,
  input  [1:0] RB,
  input  Clk,
  input  R,
  output [7:0] RD1,
  output [7:0] RD2
);

  wire demultiplexer_1_out0, R1, R2, R3;
  wire [7:0] D1, D2, D3;

  // NoConnect on demultiplexer_1_out0
  Demultiplexer #(.select(2)) demultiplexer_1 (
    .out0(demultiplexer_1_out0), .out1(R1), .out2(R2), .out3(R3), .in(WE), .sel(RD));
  Register #(.trigger("falling")) SR1 (.D(Data), .en(R1), .clk(Clk), .Q(D1), .clr(R));
  Register #(.trigger("falling")) SR2 (.D(Data), .en(R2), .clk(Clk), .Q(D2), .clr(R));
  Register #(.trigger("falling")) SR3 (.D(Data), .en(R3), .clk(Clk), .Q(D3), .clr(R));
  Multiplexer #(.select(2), .width(8)) multiplexer_1 (
    .in0({8{1'b0}}), .in1(D1), .in2(D2), .in3(D3), .out(RD1), .sel(RA));
  Multiplexer #(.select(2), .width(8)) multiplexer_2 (
    .in0({8{1'b0}}), .in1(D1), .in2(D2), .in3(D3), .out(RD2), .sel(RB));

  // Notes on the sheet:
  //   SR0
endmodule

module SPE_ULA (
  input  [7:0] RA,
  input  [7:0] RB,
  input  [2:0] ULA_Op,
  output [7:0] out_4
);

  wire [7:0] R2, R3, R4;

  // NoConnect on RA[7:4]
  // NoConnect on RB[7:4]
  // NoConnect on RB[7:4]
  // NoConnect on RA[3:0]
  Adder adder_1 (.a(RA), .b(RB), .out(R2));  // open: cin, cout
  Subtractor subtractor_1 (.a(RA), .b(RB), .out(R3));  // open: bin, bout
  assign R4 = RA & RB;  // AND_Gate and_1, 8 bits wide
  Multiplexer #(.select(3), .width(8)) multiplexer_1 (
    .in0({RB[3:0], RA[3:0]}), .in1({RA[7:4], RB[3:0]}), .in2(R2), .in3(R3), .in4(R4), .in5({8{1'b0}}),
    .in6({8{1'b0}}), .in7({8{1'b0}}), .out(out_4), .sel(ULA_Op));

  // Other names for the same wires on the sheet: R0[7:0] = {RB[3:0], RA[3:0]}; R1[7:0] = {RA[7:4], RB[3:0]}

  // Notes on the sheet:
  //   Move High
  //   Move Low
  //   Adder
  //   Subtractor
  //   AND
endmodule

module SPE_Memory_Data (
  input  [7:0] Addr,
  input  WM,
  input  Clk,
  input  [7:0] d,
  output [7:0] data
);

  RAM ram_1 (.addr(Addr), .we(WM), .oe(1'b1), .clk(Clk), .din(d), .dout(data));
endmodule

module VPE_Ctrl (
  input  [9:0] VectorSigns,
  output [1:0] ID_V,
  output [3:0] EXE_V,
  output [1:0] MEM_V,
  output [1:0] WB_V
);


  assign EXE_V = VectorSigns[7:4];
  assign ID_V = VectorSigns[9:8];
  assign MEM_V = VectorSigns[3:2];
  assign WB_V = VectorSigns[1:0];
endmodule

module VPE0_Register_Bank (
  input  [7:0] Data,
  input  [1:0] RA,
  input  WE,
  input  [1:0] RD,
  input  [1:0] RB,
  input  Clk,
  input  R,
  output [7:0] RD1,
  output [7:0] RD2
);

  wire demultiplexer_1_out0, R1, R2, R3;
  wire [7:0] D1, D2, D3;

  // NoConnect on demultiplexer_1_out0
  Demultiplexer #(.select(2)) demultiplexer_1 (
    .out0(demultiplexer_1_out0), .out1(R1), .out2(R2), .out3(R3), .in(WE), .sel(RD));
  Register #(.trigger("falling")) VR1 (.D(Data), .en(R1), .clk(Clk), .Q(D1), .clr(R));
  Register #(.trigger("falling")) VR2 (.D(Data), .en(R2), .clk(Clk), .Q(D2), .clr(R));
  Register #(.trigger("falling")) VR3 (.D(Data), .en(R3), .clk(Clk), .Q(D3), .clr(R));
  Multiplexer #(.select(2), .width(8)) multiplexer_1 (
    .in0({8{1'b0}}), .in1(D1), .in2(D2), .in3(D3), .out(RD1), .sel(RA));
  Multiplexer #(.select(2), .width(8)) multiplexer_2 (
    .in0({8{1'b0}}), .in1(D1), .in2(D2), .in3(D3), .out(RD2), .sel(RB));

  // Notes on the sheet:
  //   VR0
endmodule

module VPE1_Register_Bank (
  input  [7:0] Data,
  input  [1:0] RA,
  input  WE,
  input  [1:0] RD,
  input  [1:0] RB,
  input  Clk,
  input  R,
  output [7:0] RD1,
  output [7:0] RD2
);

  wire demultiplexer_1_out0, R1, R2, R3;
  wire [7:0] D1, D2, D3;

  // NoConnect on demultiplexer_1_out0
  Demultiplexer #(.select(2)) demultiplexer_1 (
    .out0(demultiplexer_1_out0), .out1(R1), .out2(R2), .out3(R3), .in(WE), .sel(RD));
  Register #(.trigger("falling")) VR1 (.D(Data), .en(R1), .clk(Clk), .Q(D1), .clr(R));
  Register #(.trigger("falling")) VR2 (.D(Data), .en(R2), .clk(Clk), .Q(D2), .clr(R));
  Register #(.trigger("falling")) VR3 (.D(Data), .en(R3), .clk(Clk), .Q(D3), .clr(R));
  Multiplexer #(.select(2), .width(8)) multiplexer_1 (.in0(8'h1), .in1(D1), .in2(D2), .in3(D3), .out(RD1), .sel(RA));
  Multiplexer #(.select(2), .width(8)) multiplexer_2 (.in0(8'h1), .in1(D1), .in2(D2), .in3(D3), .out(RD2), .sel(RB));

  // Notes on the sheet:
  //   VR0
endmodule

module VPE2_Register_Bank (
  input  [7:0] Data,
  input  [1:0] RA,
  input  WE,
  input  [1:0] RD,
  input  [1:0] RB,
  input  Clk,
  input  R,
  output [7:0] RD1,
  output [7:0] RD2
);

  wire demultiplexer_1_out0, R1, R2, R3;
  wire [7:0] D1, D2, D3;

  // NoConnect on demultiplexer_1_out0
  Demultiplexer #(.select(2)) demultiplexer_1 (
    .out0(demultiplexer_1_out0), .out1(R1), .out2(R2), .out3(R3), .in(WE), .sel(RD));
  Register #(.trigger("falling")) VR1 (.D(Data), .en(R1), .clk(Clk), .Q(D1), .clr(R));
  Register #(.trigger("falling")) VR2 (.D(Data), .en(R2), .clk(Clk), .Q(D2), .clr(R));
  Register #(.trigger("falling")) VR3 (.D(Data), .en(R3), .clk(Clk), .Q(D3), .clr(R));
  Multiplexer #(.select(2), .width(8)) multiplexer_1 (.in0(8'h2), .in1(D1), .in2(D2), .in3(D3), .out(RD1), .sel(RA));
  Multiplexer #(.select(2), .width(8)) multiplexer_2 (.in0(8'h2), .in1(D1), .in2(D2), .in3(D3), .out(RD2), .sel(RB));

  // Notes on the sheet:
  //   VR0
endmodule

module VPE3_Register_Bank (
  input  [7:0] Data,
  input  [1:0] RA,
  input  WE,
  input  [1:0] RD,
  input  [1:0] RB,
  input  Clk,
  input  R,
  output [7:0] RD1,
  output [7:0] RD2
);

  wire demultiplexer_1_out0, R1, R2, R3;
  wire [7:0] D1, D2, D3;

  // NoConnect on demultiplexer_1_out0
  Demultiplexer #(.select(2)) demultiplexer_1 (
    .out0(demultiplexer_1_out0), .out1(R1), .out2(R2), .out3(R3), .in(WE), .sel(RD));
  Register #(.trigger("falling")) VR1 (.D(Data), .en(R1), .clk(Clk), .Q(D1), .clr(R));
  Register #(.trigger("falling")) VR2 (.D(Data), .en(R2), .clk(Clk), .Q(D2), .clr(R));
  Register #(.trigger("falling")) VR3 (.D(Data), .en(R3), .clk(Clk), .Q(D3), .clr(R));
  Multiplexer #(.select(2), .width(8)) multiplexer_1 (.in0(8'h3), .in1(D1), .in2(D2), .in3(D3), .out(RD1), .sel(RA));
  Multiplexer #(.select(2), .width(8)) multiplexer_2 (.in0(8'h3), .in1(D1), .in2(D2), .in3(D3), .out(RD2), .sel(RB));

  // Notes on the sheet:
  //   VR0
endmodule

module VPE_ULA (
  input  [7:0] RA,
  input  [7:0] RB,
  input  [2:0] ULA_Op,
  output [7:0] out_4
);

  wire comparator_1_eq;
  wire [7:0] R2, R3, R4;

  // NoConnect on RA[7:4]
  // NoConnect on RB[7:4]
  // NoConnect on RB[7:4]
  // NoConnect on RA[3:0]
  Adder adder_1 (.a(RA), .b(RB), .out(R2));  // open: cin, cout
  Subtractor subtractor_1 (.a(RA), .b(RB), .out(R3));  // open: bin, bout
  assign R4 = {{7{comparator_1_eq}}, comparator_1_eq};  // Bit_Extender bit_extender_1
  Comparator comparator_1 (.a(RA), .b(RB), .eq(comparator_1_eq));  // open: gt, lt
  Multiplexer #(.select(3), .width(8)) multiplexer_1 (
    .in0({RB[3:0], RA[3:0]}), .in1({RA[7:4], RB[3:0]}), .in2(R2), .in3(R3), .in4(R4), .in5({8{1'b0}}),
    .in6({8{1'b0}}), .in7({8{1'b0}}), .out(out_4), .sel(ULA_Op));

  // Other names for the same wires on the sheet: R0[7:0] = {RB[3:0], RA[3:0]}; R1[7:0] = {RA[7:4], RB[3:0]}

  // Notes on the sheet:
  //   Move High
  //   Move Low
  //   Adder
  //   Subtractor
  //   Comparator
endmodule

module VPE_Memory_Data (
  input  [7:0] Addr,
  input  WM,
  input  Clk,
  input  [7:0] d,
  output [7:0] data
);

  RAM #(.trigger("falling")) ram_1 (.addr(Addr), .we(WM), .oe(1'b1), .clk(Clk), .din(d), .dout(data));
endmodule

module Stg_IF_ID (
  input  [7:0] Inst_IF,
  input  En,
  input  Clk,
  input  R,
  output [7:0] Inst_ID
);

  Register Inst (.D(Inst_IF), .en(En), .clk(Clk), .Q(Inst_ID), .clr(R));
endmodule

module Stg_ID_EX_Spe (
  input  [3:0] ExeSgn_Id,
  input  [1:0] MemSgn_Id,
  input  WbSgn_Id,
  input  [7:0] RD1_Id,
  input  [7:0] RD2_Id,
  input  [5:0] ARs_Id,
  input  [7:0] Imm_Id,
  input  Clk,
  input  R,
  output [3:0] ExeSgn_Exe,
  output [1:0] MemSgn_Exe,
  output WbSgn_Exe,
  output [7:0] RD1_Exe,
  output [7:0] RD2_Exe,
  output [5:0] ARs_Exe,
  output [7:0] Imm_Exe
);

  Register #(.width(4)) EXE (.D(ExeSgn_Id), .en(1'b1), .clk(Clk), .Q(ExeSgn_Exe), .clr(R));
  Register #(.width(2)) MEM (.D(MemSgn_Id), .en(1'b1), .clk(Clk), .Q(MemSgn_Exe), .clr(R));
  Register #(.width(1)) WB (.D(WbSgn_Id), .en(1'b1), .clk(Clk), .Q(WbSgn_Exe), .clr(R));
  Register RD1 (.D(RD1_Id), .en(1'b1), .clk(Clk), .Q(RD1_Exe), .clr(R));
  Register RD2 (.D(RD2_Id), .en(1'b1), .clk(Clk), .Q(RD2_Exe), .clr(R));
  Register #(.width(6)) AdRs (.D(ARs_Id), .en(1'b1), .clk(Clk), .Q(ARs_Exe), .clr(R));
  Register Imm (.D(Imm_Id), .en(1'b1), .clk(Clk), .Q(Imm_Exe), .clr(R));
endmodule

module Stg_ID_EX_Vpe_General (
  input  [3:0] ExeSgn_Id,
  input  [1:0] MemSgn_Id,
  input  [1:0] WbSgn_Id,
  input  [5:0] ARs_Id,
  input  [7:0] Imm_Id,
  input  Clk,
  input  R,
  output [3:0] ExeSgn_Exe,
  output [1:0] MemSgn_Exe,
  output [1:0] WbSgn_Exe,
  output [5:0] ARs_Exe,
  output [7:0] Imm_Exe
);

  Register #(.width(4)) EXE (.D(ExeSgn_Id), .en(1'b1), .clk(Clk), .Q(ExeSgn_Exe), .clr(R));
  Register #(.width(2)) MEM (.D(MemSgn_Id), .en(1'b1), .clk(Clk), .Q(MemSgn_Exe), .clr(R));
  Register #(.width(2)) WB (.D(WbSgn_Id), .en(1'b1), .clk(Clk), .Q(WbSgn_Exe), .clr(R));
  Register #(.width(6)) AdRs (.D(ARs_Id), .en(1'b1), .clk(Clk), .Q(ARs_Exe), .clr(R));
  Register Imm (.D(Imm_Id), .en(1'b1), .clk(Clk), .Q(Imm_Exe), .clr(R));
endmodule

module Stg_ID_EX_Vpe (
  input  [7:0] RD1_Id,
  input  [7:0] RD2_Id,
  input  Clk,
  input  R,
  output [7:0] RD1_Exe,
  output [7:0] RD2_Exe
);

  Register RD1 (.D(RD1_Id), .en(1'b1), .clk(Clk), .Q(RD1_Exe), .clr(R));
  Register RD2 (.D(RD2_Id), .en(1'b1), .clk(Clk), .Q(RD2_Exe), .clr(R));
endmodule

module Stg_EX_MEM_Spe (
  input  [1:0] MemSgn_Exe,
  input  WbSgn_Exe,
  input  [7:0] UlaR_Exe,
  input  [7:0] Addr_Exe,
  input  [7:0] Data_Exe,
  input  [1:0] AddrR_Exe,
  input  Clk,
  input  R,
  output [1:0] MemSgn_Mem,
  output WbSgn_Mem,
  output [7:0] UlaR_Mem,
  output [7:0] Addr_Mem,
  output [7:0] Data_Mem,
  output [1:0] AddrR_Mem
);

  Register #(.width(2)) MEM (.D(MemSgn_Exe), .en(1'b1), .clk(Clk), .Q(MemSgn_Mem), .clr(R));
  Register #(.width(1)) WB (.D(WbSgn_Exe), .en(1'b1), .clk(Clk), .Q(WbSgn_Mem), .clr(R));
  Register UlaR (.D(UlaR_Exe), .en(1'b1), .clk(Clk), .Q(UlaR_Mem), .clr(R));
  Register Addr (.D(Addr_Exe), .en(1'b1), .clk(Clk), .Q(Addr_Mem), .clr(R));
  Register Data (.D(Data_Exe), .en(1'b1), .clk(Clk), .Q(Data_Mem), .clr(R));
  Register #(.width(2)) AddrR (.D(AddrR_Exe), .en(1'b1), .clk(Clk), .Q(AddrR_Mem), .clr(R));
endmodule

module Stg_EX_MEM_VPE_General (
  input  [1:0] MemSgn_Exe,
  input  [1:0] WbSgn_Exe,
  input  [1:0] AddrR_Exe,
  input  Clk,
  input  R,
  output [1:0] MemSgn_Mem,
  output [1:0] WbSgn_Mem,
  output [1:0] AddrR_Mem
);

  Register #(.width(2)) MEM (.D(MemSgn_Exe), .en(1'b1), .clk(Clk), .Q(MemSgn_Mem), .clr(R));
  Register #(.width(2)) WB (.D(WbSgn_Exe), .en(1'b1), .clk(Clk), .Q(WbSgn_Mem), .clr(R));
  Register #(.width(2)) AddrR (.D(AddrR_Exe), .en(1'b1), .clk(Clk), .Q(AddrR_Mem), .clr(R));
endmodule

module Stg_EX_MEM_Vpe (
  input  [7:0] UlaR_Exe,
  input  [7:0] Addr_Exe,
  input  [7:0] Data_Exe,
  input  Clk,
  input  R,
  output [7:0] UlaR_Mem,
  output [7:0] Addr_Mem,
  output [7:0] Data_Mem
);

  Register UlaR (.D(UlaR_Exe), .en(1'b1), .clk(Clk), .Q(UlaR_Mem), .clr(R));
  Register Addr (.D(Addr_Exe), .en(1'b1), .clk(Clk), .Q(Addr_Mem), .clr(R));
  Register Data (.D(Data_Exe), .en(1'b1), .clk(Clk), .Q(Data_Mem), .clr(R));
endmodule

module Stg_MEM_WB_Spe (
  input  WbSgn_Mem,
  input  [7:0] Data_Mem,
  input  [1:0] AddrR_Mem,
  input  Clk,
  input  R,
  output WbSgn_WB,
  output [7:0] Data_WB,
  output [1:0] AddrR_WB
);

  Register #(.width(1)) WB (.D(WbSgn_Mem), .en(1'b1), .clk(Clk), .Q(WbSgn_WB), .clr(R));
  Register Data (.D(Data_Mem), .en(1'b1), .clk(Clk), .Q(Data_WB), .clr(R));
  Register #(.width(2)) AddrR (.D(AddrR_Mem), .en(1'b1), .clk(Clk), .Q(AddrR_WB), .clr(R));
endmodule

module Stg_MEM_WB_Vpe_General (
  input  [1:0] WbSgn_Mem,
  input  [1:0] AddrR_Mem,
  input  Clk,
  input  R,
  output [1:0] WbSgn_WB,
  output [1:0] AddrR_WB
);

  Register #(.width(2)) WB (.D(WbSgn_Mem), .en(1'b1), .clk(Clk), .Q(WbSgn_WB), .clr(R));
  Register #(.width(2)) AddrR (.D(AddrR_Mem), .en(1'b1), .clk(Clk), .Q(AddrR_WB), .clr(R));
endmodule

module Stg_MEM_WB_Vpe (
  input  [7:0] NPtr_Mem,
  input  [7:0] Data_Mem,
  input  Clk,
  input  R,
  output [7:0] NPtr_WB,
  output [7:0] Data_WB
);

  Register NPtr (.D(NPtr_Mem), .en(1'b1), .clk(Clk), .Q(NPtr_WB), .clr(R));
  Register Data (.D(Data_Mem), .en(1'b1), .clk(Clk), .Q(Data_WB), .clr(R));
endmodule

module ForwardingULA_Unit (
  input  WE_ExMem,
  input  WE_MemWb,
  input  [1:0] Rd_MemWb,
  input  [1:0] Rd_ExMem,
  input  [1:0] Rb,
  input  [1:0] Ra,
  output [1:0] Forw_A,
  output [1:0] Forw_B
);

  wire comparator_1_eq, comparator_2_eq, comparator_3_eq, comparator_4_eq, comparator_5_eq, comparator_6_eq;
  wire [0:0] and_2_out, and_4_out;
  wire [1:1] and_1_out, and_3_out;

  Comparator #(.mode("unsigned"), .width(2)) comparator_1 (.a(Ra), .b(Rd_ExMem), .eq(comparator_1_eq));  // open: gt, lt
  Comparator #(.mode("unsigned"), .width(2)) comparator_2 (.a(Ra), .b(Rd_MemWb), .eq(comparator_2_eq));  // open: gt, lt
  Comparator #(.mode("unsigned"), .width(2)) comparator_3 (.a(Rb), .b(Rd_ExMem), .eq(comparator_3_eq));  // open: gt, lt
  Comparator #(.mode("unsigned"), .width(2)) comparator_4 (.a(Rb), .b(Rd_MemWb), .eq(comparator_4_eq));  // open: gt, lt
  and and_1 (and_1_out[1], comparator_1_eq, WE_ExMem);
  and and_2 (and_2_out[0], comparator_2_eq, WE_MemWb);
  and and_3 (and_3_out[1], comparator_3_eq, WE_ExMem);
  and and_4 (and_4_out[0], comparator_4_eq, WE_MemWb);
  Comparator #(.mode("unsigned"), .width(2)) comparator_5 (
    .a({and_1_out[1], 1'b0}), .b(2'b00), .eq(comparator_5_eq));  // open: gt, lt
  Comparator #(.mode("unsigned"), .width(2)) comparator_6 (
    .a({and_3_out[1], 1'b0}), .b(2'b00), .eq(comparator_6_eq));  // open: gt, lt
  Multiplexer #(.width(2)) multiplexer_1 (
    .in0({and_1_out[1], 1'b0}), .in1({1'b0, and_2_out[0]}), .out(Forw_A), .sel(comparator_5_eq));
  Multiplexer #(.width(2)) multiplexer_2 (
    .in0({and_3_out[1], 1'b0}), .in1({1'b0, and_4_out[0]}), .out(Forw_B), .sel(comparator_6_eq));
endmodule

module ForwardingBranch_Unit (
  input  WE_IdEx,
  input  WE_ExMem,
  input  [1:0] Rd_ExMem,
  input  [1:0] Rd_IdEx,
  input  [1:0] Ra_id,
  output [1:0] Forw_Br
);

  wire comparator_1_eq, comparator_2_eq, comparator_3_eq;
  wire [0:0] and_2_out;
  wire [1:1] and_1_out;

  Comparator #(.mode("unsigned"), .width(2)) comparator_1 (
    .a(Ra_id), .b(Rd_IdEx), .eq(comparator_1_eq));  // open: gt, lt
  Comparator #(.mode("unsigned"), .width(2)) comparator_2 (
    .a(Ra_id), .b(Rd_ExMem), .eq(comparator_2_eq));  // open: gt, lt
  and and_1 (and_1_out[1], comparator_1_eq, WE_IdEx);
  and and_2 (and_2_out[0], comparator_2_eq, WE_ExMem);
  Comparator #(.mode("unsigned"), .width(2)) comparator_3 (
    .a({and_1_out[1], 1'b0}), .b(2'b00), .eq(comparator_3_eq));  // open: gt, lt
  Multiplexer #(.width(2)) multiplexer_1 (
    .in0({and_1_out[1], 1'b0}), .in1({1'b0, and_2_out[0]}), .out(Forw_Br), .sel(comparator_3_eq));
endmodule

module Hazard_Unit (
  input  [1:0] RD_ex,
  input  [1:0] RB_id,
  input  [1:0] RA_id,
  input  MemRead,
  input  Br,
  output hnop,
  output EN
);

  wire and_1_out, comparator_1_eq, comparator_2_eq, or_1_out;

  Comparator #(.mode("unsigned"), .width(2)) comparator_1 (.a(RA_id), .b(RD_ex), .eq(comparator_1_eq));  // open: gt, lt
  Comparator #(.mode("unsigned"), .width(2)) comparator_2 (.a(RB_id), .b(RD_ex), .eq(comparator_2_eq));  // open: gt, lt
  or or_1 (or_1_out, comparator_1_eq, comparator_2_eq);
  and and_1 (and_1_out, or_1_out, MemRead);
  or or_2 (hnop, and_1_out, Br);
  not not_1 (EN, and_1_out);
endmodule
