// Logisim project t3.circ as structural Verilog: 9 circuits, main circuit main
module main (
);

  wire branch, clk, reset;
  wire [7:0] B, imm8;
  wire [31:0] adder_1_out, B32, imm32, multiplexer_1_out, multiplexer_2_out, PC;

  Button u_reset (.out(reset));
  Clock #(.highDuration(2), .lowDuration(2), .phaseOffset(1)) clock_1 (.out(clk));
  Multiplexer #(.width(32)) multiplexer_1 (.in0(32'h20), .in1(imm32), .out(multiplexer_1_out), .sel(branch));
  extSinal32bits extsinal32bits_1 (.imm8(imm8), .imm32(imm32));
  extSinal32bits extsinal32bits_2 (.imm8(B), .imm32(B32));
  Adder #(.width(32)) adder_1 (.a(PC), .b(multiplexer_1_out), .out(adder_1_out));  // open: cin, cout
  RAM MemInst ();  // open: addr, we, oe, clk, din, dout
  Multiplexer #(.width(32)) multiplexer_2 (.in0(adder_1_out), .in1(B32), .out(multiplexer_2_out));  // open: sel
  Register #(.width(32)) u_Pc (.D(multiplexer_2_out), .en(1'b1), .clk(clk), .Q(PC), .clr(reset));
  extSinal8bits extsinal8bits_1 ();  // open: imm4, imm8
  movhighmovlow movhighmovlow_1 ();  // open: A, imm, Seletor, R
  BancoReg bancoreg_1 ();  // open: clk, d, w, SelW, SelA, SelB, reset, A, B
  ULA ula_1 ();  // open: A, B, Seletor, brzr, R
  ULA ula_2 ();  // open: A, B, Seletor, brzr, R
  ROM rom_1 ();  // open: addr, data
  RAM MemDados ();  // open: addr, we, oe, clk, din, dout

  // Notes on the sheet:
  //   brzi
  //   brzr e jr
  //   TODO alterar com os sinais de controle
  //   TODO ver como fazer a mem com pc32bits
  //   MemInst
  //   TODO um banreg so ou mais
  //   MemControle
  //   MemDados
endmodule

module BancoReg (
  input  clk,
  input  [7:0] d,
  input  w,
  input  [1:0] SelW,
  input  [1:0] SelA,
  input  [1:0] SelB,
  input  reset,
  output [7:0] A,
  output [7:0] B
);

  wire w0, w1, w2, w3;
  wire [7:0] l0, l1, l2, l3;

  Demultiplexer #(.select(2)) demultiplexer_1 (.out0(w0), .out1(w1), .out2(w2), .out3(w3), .in(w), .sel(SelW));
  Multiplexer #(.select(2), .width(8)) multiplexer_1 (.in0(l0), .in1(l1), .in2(l2), .in3(l3), .out(A), .sel(SelA));
  Multiplexer #(.select(2), .width(8)) multiplexer_2 (.in0(l0), .in1(l1), .in2(l2), .in3(l3), .out(B), .sel(SelB));
  Register r0 (.D(d), .en(w0), .clk(clk), .Q(l0), .clr(reset));
  Register r1 (.D(d), .en(w1), .clk(clk), .Q(l1), .clr(reset));
  Register r2 (.D(d), .en(w2), .clk(clk), .Q(l2), .clr(reset));
  Register r3 (.D(d), .en(w3), .clk(clk), .Q(l3), .clr(reset));

  // Other names for the same wires on the sheet: data[7:0] = d

  // Notes on the sheet:
  //   Escrita
  //   Leitura A
  //   Leitura B
endmodule

module extSinal8bits (
  input  [3:0] imm4,
  output [7:0] imm8
);


  assign imm8 = {{5{imm4[3]}}, imm4[2:0]};
endmodule

module ULA (
  input  [7:0] A,
  input  [7:0] B,
  input  [2:0] Seletor,
  output brzr,
  output [7:0] R
);

  wire [0:0] R3;
  wire [7:0] R0, R1, R2, R4, R5, R6, R7;

  Multiplexer #(.select(3), .width(8)) multiplexer_1 (
    .in0(R0), .in1(R1), .in2(R2), .in3({{7{1'b0}}, R3[0]}), .in4(R4), .in5(R5), .in6(R6), .in7(R7), .out(R),
    .sel(Seletor));
  Adder adder_1 (.a(A), .b(B), .out(R0));  // open: cin, cout
  Subtractor subtractor_1 (.a(A), .b(B), .out(R1));  // open: bin, bout
  assign R2 = A | B;  // OR_Gate or_1, 8 bits wide
  nor nor_1 (R3[0], B[0], B[1], B[2], B[3], B[4], B[5], B[6], B[7]);
  assign R6 = A ^ B;  // XOR_Gate xor_1, 8 bits wide
  slr slr_1 (.A(A), .B(B), .R(R4));
  srr srr_1 (.A(A), .B(B), .R(R5));
  Comparator comparator_1 (.a(A), .b({8{1'b0}}), .eq(brzr));  // open: gt, lt

  // Notes on the sheet:
  //   Add
  //   Sub
endmodule

module slr (
  input  [7:0] A,
  input  [7:0] B,
  output [7:0] R
);

  wire multiplexer_1_out, multiplexer_2_out, multiplexer_3_out, multiplexer_4_out, multiplexer_5_out,
       multiplexer_6_out, multiplexer_7_out, multiplexer_8_out, multiplexer_9_out, multiplexer_10_out,
       multiplexer_11_out, multiplexer_12_out, multiplexer_13_out, multiplexer_14_out, multiplexer_15_out,
       multiplexer_16_out, multiplexer_17_out, multiplexer_18_out, multiplexer_19_out, multiplexer_20_out,
       multiplexer_21_out, multiplexer_22_out, multiplexer_23_out, multiplexer_24_out, or_1_out;

  Multiplexer multiplexer_1 (.in0(A[0]), .in1(1'b0), .out(multiplexer_1_out), .sel(B[0]));
  Multiplexer multiplexer_2 (.in0(A[1]), .in1(A[0]), .out(multiplexer_2_out), .sel(B[0]));
  Multiplexer multiplexer_3 (.in0(A[2]), .in1(A[1]), .out(multiplexer_3_out), .sel(B[0]));
  Multiplexer multiplexer_4 (.in0(A[3]), .in1(A[2]), .out(multiplexer_4_out), .sel(B[0]));
  Multiplexer multiplexer_5 (.in0(A[4]), .in1(A[3]), .out(multiplexer_5_out), .sel(B[0]));
  Multiplexer multiplexer_6 (.in0(A[5]), .in1(A[4]), .out(multiplexer_6_out), .sel(B[0]));
  Multiplexer multiplexer_7 (.in0(A[6]), .in1(A[5]), .out(multiplexer_7_out), .sel(B[0]));
  Multiplexer multiplexer_8 (.in0(A[7]), .in1(A[6]), .out(multiplexer_8_out), .sel(B[0]));
  Multiplexer multiplexer_9 (.in0(multiplexer_1_out), .in1(1'b0), .out(multiplexer_9_out), .sel(B[1]));
  Multiplexer multiplexer_10 (.in0(multiplexer_2_out), .in1(1'b0), .out(multiplexer_10_out), .sel(B[1]));
  Multiplexer multiplexer_11 (.in0(multiplexer_3_out), .in1(multiplexer_1_out), .out(multiplexer_11_out), .sel(B[1]));
  Multiplexer multiplexer_12 (.in0(multiplexer_4_out), .in1(multiplexer_2_out), .out(multiplexer_12_out), .sel(B[1]));
  Multiplexer multiplexer_13 (.in0(multiplexer_5_out), .in1(multiplexer_3_out), .out(multiplexer_13_out), .sel(B[1]));
  Multiplexer multiplexer_14 (.in0(multiplexer_6_out), .in1(multiplexer_4_out), .out(multiplexer_14_out), .sel(B[1]));
  Multiplexer multiplexer_15 (.in0(multiplexer_7_out), .in1(multiplexer_5_out), .out(multiplexer_15_out), .sel(B[1]));
  Multiplexer multiplexer_16 (.in0(multiplexer_8_out), .in1(multiplexer_6_out), .out(multiplexer_16_out), .sel(B[1]));
  Multiplexer multiplexer_17 (.in0(multiplexer_9_out), .in1(1'b0), .out(multiplexer_17_out), .sel(B[2]));
  Multiplexer multiplexer_18 (.in0(multiplexer_10_out), .in1(1'b0), .out(multiplexer_18_out), .sel(B[2]));
  Multiplexer multiplexer_19 (.in0(multiplexer_11_out), .in1(1'b0), .out(multiplexer_19_out), .sel(B[2]));
  Multiplexer multiplexer_20 (.in0(multiplexer_12_out), .in1(1'b0), .out(multiplexer_20_out), .sel(B[2]));
  Multiplexer multiplexer_21 (.in0(multiplexer_13_out), .in1(multiplexer_9_out), .out(multiplexer_21_out), .sel(B[2]));
  Multiplexer multiplexer_22 (.in0(multiplexer_14_out), .in1(multiplexer_10_out), .out(multiplexer_22_out), .sel(B[2]));
  Multiplexer multiplexer_23 (.in0(multiplexer_15_out), .in1(multiplexer_11_out), .out(multiplexer_23_out), .sel(B[2]));
  Multiplexer multiplexer_24 (.in0(multiplexer_16_out), .in1(multiplexer_12_out), .out(multiplexer_24_out), .sel(B[2]));
  Multiplexer multiplexer_25 (.in0(multiplexer_17_out), .in1(1'b0), .out(R[0]), .sel(or_1_out));
  Multiplexer multiplexer_26 (.in0(multiplexer_18_out), .in1(1'b0), .out(R[1]), .sel(or_1_out));
  Multiplexer multiplexer_27 (.in0(multiplexer_19_out), .in1(1'b0), .out(R[2]), .sel(or_1_out));
  Multiplexer multiplexer_28 (.in0(multiplexer_20_out), .in1(1'b0), .out(R[3]), .sel(or_1_out));
  Multiplexer multiplexer_29 (.in0(multiplexer_21_out), .in1(1'b0), .out(R[4]), .sel(or_1_out));
  Multiplexer multiplexer_30 (.in0(multiplexer_22_out), .in1(1'b0), .out(R[5]), .sel(or_1_out));
  Multiplexer multiplexer_31 (.in0(multiplexer_23_out), .in1(1'b0), .out(R[6]), .sel(or_1_out));
  Multiplexer multiplexer_32 (.in0(multiplexer_24_out), .in1(1'b0), .out(R[7]), .sel(or_1_out));
  or or_1 (or_1_out, B[7], B[6], B[5], B[4], B[3]);

  // Other names for the same wires on the sheet: s0 = R[0]; s1 = R[1]; s2 = R[2]; s3 = R[3]; s4 = R[4]; s5 = R[5];
  //   s6 = R[6]; s7 = R[7]
endmodule

module srr (
  input  [7:0] A,
  input  [7:0] B,
  output [7:0] R
);

  wire multiplexer_1_out, multiplexer_2_out, multiplexer_3_out, multiplexer_4_out, multiplexer_5_out,
       multiplexer_6_out, multiplexer_7_out, multiplexer_8_out, multiplexer_9_out, multiplexer_10_out,
       multiplexer_11_out, multiplexer_12_out, multiplexer_13_out, multiplexer_14_out, multiplexer_15_out,
       multiplexer_16_out, multiplexer_17_out, multiplexer_18_out, multiplexer_19_out, multiplexer_20_out,
       multiplexer_21_out, multiplexer_22_out, multiplexer_23_out, multiplexer_24_out, or_1_out;

  Multiplexer multiplexer_1 (.in0(A[0]), .in1(A[1]), .out(multiplexer_1_out), .sel(B[0]));
  Multiplexer multiplexer_2 (.in0(A[1]), .in1(A[2]), .out(multiplexer_2_out), .sel(B[0]));
  Multiplexer multiplexer_3 (.in0(A[2]), .in1(A[3]), .out(multiplexer_3_out), .sel(B[0]));
  Multiplexer multiplexer_4 (.in0(A[3]), .in1(A[4]), .out(multiplexer_4_out), .sel(B[0]));
  Multiplexer multiplexer_5 (.in0(A[4]), .in1(A[5]), .out(multiplexer_5_out), .sel(B[0]));
  Multiplexer multiplexer_6 (.in0(A[5]), .in1(A[6]), .out(multiplexer_6_out), .sel(B[0]));
  Multiplexer multiplexer_7 (.in0(A[6]), .in1(A[7]), .out(multiplexer_7_out), .sel(B[0]));
  Multiplexer multiplexer_8 (.in0(A[7]), .in1(1'b0), .out(multiplexer_8_out), .sel(B[0]));
  Multiplexer multiplexer_9 (.in0(multiplexer_1_out), .in1(multiplexer_3_out), .out(multiplexer_9_out), .sel(B[1]));
  Multiplexer multiplexer_10 (.in0(multiplexer_2_out), .in1(multiplexer_4_out), .out(multiplexer_10_out), .sel(B[1]));
  Multiplexer multiplexer_11 (.in0(multiplexer_3_out), .in1(multiplexer_5_out), .out(multiplexer_11_out), .sel(B[1]));
  Multiplexer multiplexer_12 (.in0(multiplexer_4_out), .in1(multiplexer_6_out), .out(multiplexer_12_out), .sel(B[1]));
  Multiplexer multiplexer_13 (.in0(multiplexer_5_out), .in1(multiplexer_7_out), .out(multiplexer_13_out), .sel(B[1]));
  Multiplexer multiplexer_14 (.in0(multiplexer_6_out), .in1(multiplexer_8_out), .out(multiplexer_14_out), .sel(B[1]));
  Multiplexer multiplexer_15 (.in0(multiplexer_7_out), .in1(1'b0), .out(multiplexer_15_out), .sel(B[1]));
  Multiplexer multiplexer_16 (.in0(multiplexer_8_out), .in1(1'b0), .out(multiplexer_16_out), .sel(B[1]));
  Multiplexer multiplexer_17 (.in0(multiplexer_9_out), .in1(multiplexer_13_out), .out(multiplexer_17_out), .sel(B[2]));
  Multiplexer multiplexer_18 (.in0(multiplexer_10_out), .in1(multiplexer_14_out), .out(multiplexer_18_out), .sel(B[2]));
  Multiplexer multiplexer_19 (.in0(multiplexer_11_out), .in1(multiplexer_15_out), .out(multiplexer_19_out), .sel(B[2]));
  Multiplexer multiplexer_20 (.in0(multiplexer_12_out), .in1(multiplexer_16_out), .out(multiplexer_20_out), .sel(B[2]));
  Multiplexer multiplexer_21 (.in0(multiplexer_13_out), .in1(1'b0), .out(multiplexer_21_out), .sel(B[2]));
  Multiplexer multiplexer_22 (.in0(multiplexer_14_out), .in1(1'b0), .out(multiplexer_22_out), .sel(B[2]));
  Multiplexer multiplexer_23 (.in0(multiplexer_15_out), .in1(1'b0), .out(multiplexer_23_out), .sel(B[2]));
  Multiplexer multiplexer_24 (.in0(multiplexer_16_out), .in1(1'b0), .out(multiplexer_24_out), .sel(B[2]));
  Multiplexer multiplexer_25 (.in0(multiplexer_17_out), .in1(1'b0), .out(R[0]), .sel(or_1_out));
  Multiplexer multiplexer_26 (.in0(multiplexer_18_out), .in1(1'b0), .out(R[1]), .sel(or_1_out));
  Multiplexer multiplexer_27 (.in0(multiplexer_19_out), .in1(1'b0), .out(R[2]), .sel(or_1_out));
  Multiplexer multiplexer_28 (.in0(multiplexer_20_out), .in1(1'b0), .out(R[3]), .sel(or_1_out));
  Multiplexer multiplexer_29 (.in0(multiplexer_21_out), .in1(1'b0), .out(R[4]), .sel(or_1_out));
  Multiplexer multiplexer_30 (.in0(multiplexer_22_out), .in1(1'b0), .out(R[5]), .sel(or_1_out));
  Multiplexer multiplexer_31 (.in0(multiplexer_23_out), .in1(1'b0), .out(R[6]), .sel(or_1_out));
  Multiplexer multiplexer_32 (.in0(multiplexer_24_out), .in1(1'b0), .out(R[7]), .sel(or_1_out));
  or or_1 (or_1_out, B[7], B[6], B[5], B[4], B[3]);

  // Other names for the same wires on the sheet: s0 = R[0]; s1 = R[1]; s2 = R[2]; s3 = R[3]; s4 = R[4]; s5 = R[5];
  //   s6 = R[6]; s7 = R[7]
endmodule

module movhighmovlow (
  input  [7:0] A,
  input  [3:0] imm,
  input  Seletor,
  output [7:0] R
);

  Multiplexer #(.width(8)) multiplexer_1 (.in0({imm, A[3:0]}), .in1({A[7:4], imm}), .out(R), .sel(Seletor));

  // Notes on the sheet:
  //   High
  //   Low
endmodule

module slr32bits (
  input  [31:0] A,
  input  [31:0] B,
  output [31:0] sDesl
);

  wire multiplexer_1_out, multiplexer_2_out, multiplexer_3_out, multiplexer_4_out, multiplexer_5_out,
       multiplexer_6_out, multiplexer_7_out, multiplexer_8_out, multiplexer_9_out, multiplexer_10_out,
       multiplexer_11_out, multiplexer_12_out, multiplexer_13_out, multiplexer_14_out, multiplexer_15_out,
       multiplexer_16_out, multiplexer_17_out, multiplexer_18_out, multiplexer_19_out, multiplexer_20_out,
       multiplexer_21_out, multiplexer_22_out, multiplexer_23_out, multiplexer_24_out, multiplexer_25_out,
       multiplexer_26_out, multiplexer_27_out, multiplexer_28_out, multiplexer_29_out, multiplexer_30_out,
       multiplexer_31_out, multiplexer_32_out, multiplexer_33_out, multiplexer_34_out, multiplexer_35_out,
       multiplexer_36_out, multiplexer_37_out, multiplexer_38_out, multiplexer_39_out, multiplexer_40_out,
       multiplexer_41_out, multiplexer_42_out, multiplexer_43_out, multiplexer_44_out, multiplexer_45_out,
       multiplexer_46_out, multiplexer_47_out, multiplexer_48_out, multiplexer_49_out, multiplexer_50_out,
       multiplexer_51_out, multiplexer_52_out, multiplexer_53_out, multiplexer_54_out, multiplexer_55_out,
       multiplexer_56_out, multiplexer_57_out, multiplexer_58_out, multiplexer_59_out, multiplexer_60_out,
       multiplexer_61_out, multiplexer_62_out, multiplexer_63_out, multiplexer_64_out, multiplexer_65_out,
       multiplexer_66_out, multiplexer_67_out, multiplexer_68_out, multiplexer_69_out, multiplexer_70_out,
       multiplexer_71_out, multiplexer_72_out, multiplexer_73_out, multiplexer_74_out, multiplexer_75_out,
       multiplexer_76_out, multiplexer_77_out, multiplexer_78_out, multiplexer_79_out, multiplexer_80_out,
       multiplexer_81_out, multiplexer_82_out, multiplexer_83_out, multiplexer_84_out, multiplexer_85_out,
       multiplexer_86_out, multiplexer_87_out, multiplexer_88_out, multiplexer_89_out, multiplexer_90_out,
       multiplexer_91_out, multiplexer_92_out, multiplexer_93_out, multiplexer_94_out, multiplexer_95_out,
       multiplexer_96_out, multiplexer_97_out, multiplexer_98_out, multiplexer_99_out, multiplexer_100_out,
       multiplexer_101_out, multiplexer_102_out, multiplexer_103_out, multiplexer_104_out,
       multiplexer_105_out, multiplexer_106_out, multiplexer_107_out, multiplexer_108_out,
       multiplexer_109_out, multiplexer_110_out, multiplexer_111_out, multiplexer_112_out,
       multiplexer_113_out, multiplexer_114_out, multiplexer_115_out, multiplexer_116_out,
       multiplexer_117_out, multiplexer_118_out, multiplexer_119_out, multiplexer_120_out,
       multiplexer_121_out, multiplexer_122_out, multiplexer_123_out, multiplexer_124_out,
       multiplexer_125_out, multiplexer_126_out, multiplexer_127_out, multiplexer_128_out,
       multiplexer_129_out, multiplexer_130_out, multiplexer_131_out, multiplexer_132_out,
       multiplexer_133_out, multiplexer_134_out, multiplexer_135_out, multiplexer_136_out,
       multiplexer_137_out, multiplexer_138_out, multiplexer_139_out, multiplexer_140_out,
       multiplexer_141_out, multiplexer_142_out, multiplexer_143_out, multiplexer_144_out,
       multiplexer_145_out, multiplexer_146_out, multiplexer_147_out, multiplexer_148_out,
       multiplexer_149_out, multiplexer_150_out, multiplexer_151_out, multiplexer_152_out,
       multiplexer_153_out, multiplexer_154_out, multiplexer_155_out, multiplexer_156_out,
       multiplexer_157_out, multiplexer_158_out, multiplexer_159_out, multiplexer_160_out, or_1_out;

  Multiplexer multiplexer_1 (.in0(A[0]), .in1(1'b0), .out(multiplexer_1_out), .sel(B[0]));
  Multiplexer multiplexer_2 (.in0(A[1]), .in1(A[0]), .out(multiplexer_2_out), .sel(B[0]));
  Multiplexer multiplexer_3 (.in0(A[2]), .in1(A[1]), .out(multiplexer_3_out), .sel(B[0]));
  Multiplexer multiplexer_4 (.in0(A[3]), .in1(A[2]), .out(multiplexer_4_out), .sel(B[0]));
  Multiplexer multiplexer_5 (.in0(A[4]), .in1(A[3]), .out(multiplexer_5_out), .sel(B[0]));
  Multiplexer multiplexer_6 (.in0(A[5]), .in1(A[4]), .out(multiplexer_6_out), .sel(B[0]));
  Multiplexer multiplexer_7 (.in0(A[6]), .in1(A[5]), .out(multiplexer_7_out), .sel(B[0]));
  Multiplexer multiplexer_8 (.in0(A[7]), .in1(A[6]), .out(multiplexer_8_out), .sel(B[0]));
  Multiplexer multiplexer_9 (.in0(A[8]), .in1(A[7]), .out(multiplexer_9_out), .sel(B[0]));
  Multiplexer multiplexer_10 (.in0(A[9]), .in1(A[8]), .out(multiplexer_10_out), .sel(B[0]));
  Multiplexer multiplexer_11 (.in0(A[10]), .in1(A[9]), .out(multiplexer_11_out), .sel(B[0]));
  Multiplexer multiplexer_12 (.in0(A[11]), .in1(A[10]), .out(multiplexer_12_out), .sel(B[0]));
  Multiplexer multiplexer_13 (.in0(A[12]), .in1(A[11]), .out(multiplexer_13_out), .sel(B[0]));
  Multiplexer multiplexer_14 (.in0(A[13]), .in1(A[12]), .out(multiplexer_14_out), .sel(B[0]));
  Multiplexer multiplexer_15 (.in0(A[14]), .in1(A[13]), .out(multiplexer_15_out), .sel(B[0]));
  Multiplexer multiplexer_16 (.in0(A[15]), .in1(A[14]), .out(multiplexer_16_out), .sel(B[0]));
  Multiplexer multiplexer_17 (.in0(A[16]), .in1(A[15]), .out(multiplexer_17_out), .sel(B[0]));
  Multiplexer multiplexer_18 (.in0(A[17]), .in1(A[16]), .out(multiplexer_18_out), .sel(B[0]));
  Multiplexer multiplexer_19 (.in0(A[18]), .in1(A[17]), .out(multiplexer_19_out), .sel(B[0]));
  Multiplexer multiplexer_20 (.in0(A[19]), .in1(A[18]), .out(multiplexer_20_out), .sel(B[0]));
  Multiplexer multiplexer_21 (.in0(A[20]), .in1(A[19]), .out(multiplexer_21_out), .sel(B[0]));
  Multiplexer multiplexer_22 (.in0(A[21]), .in1(A[20]), .out(multiplexer_22_out), .sel(B[0]));
  Multiplexer multiplexer_23 (.in0(A[22]), .in1(A[21]), .out(multiplexer_23_out), .sel(B[0]));
  Multiplexer multiplexer_24 (.in0(A[23]), .in1(A[22]), .out(multiplexer_24_out), .sel(B[0]));
  Multiplexer multiplexer_25 (.in0(A[24]), .in1(A[23]), .out(multiplexer_25_out), .sel(B[0]));
  Multiplexer multiplexer_26 (.in0(A[25]), .in1(A[24]), .out(multiplexer_26_out), .sel(B[0]));
  Multiplexer multiplexer_27 (.in0(A[26]), .in1(A[25]), .out(multiplexer_27_out), .sel(B[0]));
  Multiplexer multiplexer_28 (.in0(A[27]), .in1(A[26]), .out(multiplexer_28_out), .sel(B[0]));
  Multiplexer multiplexer_29 (.in0(A[28]), .in1(A[27]), .out(multiplexer_29_out), .sel(B[0]));
  Multiplexer multiplexer_30 (.in0(A[29]), .in1(A[28]), .out(multiplexer_30_out), .sel(B[0]));
  Multiplexer multiplexer_31 (.in0(A[30]), .in1(A[29]), .out(multiplexer_31_out), .sel(B[0]));
  Multiplexer multiplexer_32 (.in0(A[31]), .in1(A[30]), .out(multiplexer_32_out), .sel(B[0]));
  Multiplexer multiplexer_33 (.in0(multiplexer_1_out), .in1(1'b0), .out(multiplexer_33_out), .sel(B[1]));
  Multiplexer multiplexer_34 (.in0(multiplexer_2_out), .in1(1'b0), .out(multiplexer_34_out), .sel(B[1]));
  Multiplexer multiplexer_35 (.in0(multiplexer_3_out), .in1(multiplexer_1_out), .out(multiplexer_35_out), .sel(B[1]));
  Multiplexer multiplexer_36 (.in0(multiplexer_4_out), .in1(multiplexer_2_out), .out(multiplexer_36_out), .sel(B[1]));
  Multiplexer multiplexer_37 (.in0(multiplexer_5_out), .in1(multiplexer_3_out), .out(multiplexer_37_out), .sel(B[1]));
  Multiplexer multiplexer_38 (.in0(multiplexer_6_out), .in1(multiplexer_4_out), .out(multiplexer_38_out), .sel(B[1]));
  Multiplexer multiplexer_39 (.in0(multiplexer_7_out), .in1(multiplexer_5_out), .out(multiplexer_39_out), .sel(B[1]));
  Multiplexer multiplexer_40 (.in0(multiplexer_8_out), .in1(multiplexer_6_out), .out(multiplexer_40_out), .sel(B[1]));
  Multiplexer multiplexer_41 (.in0(multiplexer_9_out), .in1(multiplexer_7_out), .out(multiplexer_41_out), .sel(B[1]));
  Multiplexer multiplexer_42 (.in0(multiplexer_10_out), .in1(multiplexer_8_out), .out(multiplexer_42_out), .sel(B[1]));
  Multiplexer multiplexer_43 (.in0(multiplexer_11_out), .in1(multiplexer_9_out), .out(multiplexer_43_out), .sel(B[1]));
  Multiplexer multiplexer_44 (.in0(multiplexer_12_out), .in1(multiplexer_10_out), .out(multiplexer_44_out), .sel(B[1]));
  Multiplexer multiplexer_45 (.in0(multiplexer_13_out), .in1(multiplexer_11_out), .out(multiplexer_45_out), .sel(B[1]));
  Multiplexer multiplexer_46 (.in0(multiplexer_14_out), .in1(multiplexer_12_out), .out(multiplexer_46_out), .sel(B[1]));
  Multiplexer multiplexer_47 (.in0(multiplexer_15_out), .in1(multiplexer_13_out), .out(multiplexer_47_out), .sel(B[1]));
  Multiplexer multiplexer_48 (.in0(multiplexer_16_out), .in1(multiplexer_14_out), .out(multiplexer_48_out), .sel(B[1]));
  Multiplexer multiplexer_49 (.in0(multiplexer_17_out), .in1(multiplexer_15_out), .out(multiplexer_49_out), .sel(B[1]));
  Multiplexer multiplexer_50 (.in0(multiplexer_18_out), .in1(multiplexer_16_out), .out(multiplexer_50_out), .sel(B[1]));
  Multiplexer multiplexer_51 (.in0(multiplexer_19_out), .in1(multiplexer_17_out), .out(multiplexer_51_out), .sel(B[1]));
  Multiplexer multiplexer_52 (.in0(multiplexer_20_out), .in1(multiplexer_18_out), .out(multiplexer_52_out), .sel(B[1]));
  Multiplexer multiplexer_53 (.in0(multiplexer_21_out), .in1(multiplexer_19_out), .out(multiplexer_53_out), .sel(B[1]));
  Multiplexer multiplexer_54 (.in0(multiplexer_22_out), .in1(multiplexer_20_out), .out(multiplexer_54_out), .sel(B[1]));
  Multiplexer multiplexer_55 (.in0(multiplexer_23_out), .in1(multiplexer_21_out), .out(multiplexer_55_out), .sel(B[1]));
  Multiplexer multiplexer_56 (.in0(multiplexer_24_out), .in1(multiplexer_22_out), .out(multiplexer_56_out), .sel(B[1]));
  Multiplexer multiplexer_57 (.in0(multiplexer_25_out), .in1(multiplexer_23_out), .out(multiplexer_57_out), .sel(B[1]));
  Multiplexer multiplexer_58 (.in0(multiplexer_26_out), .in1(multiplexer_24_out), .out(multiplexer_58_out), .sel(B[1]));
  Multiplexer multiplexer_59 (.in0(multiplexer_27_out), .in1(multiplexer_25_out), .out(multiplexer_59_out), .sel(B[1]));
  Multiplexer multiplexer_60 (.in0(multiplexer_28_out), .in1(multiplexer_26_out), .out(multiplexer_60_out), .sel(B[1]));
  Multiplexer multiplexer_61 (.in0(multiplexer_29_out), .in1(multiplexer_27_out), .out(multiplexer_61_out), .sel(B[1]));
  Multiplexer multiplexer_62 (.in0(multiplexer_30_out), .in1(multiplexer_28_out), .out(multiplexer_62_out), .sel(B[1]));
  Multiplexer multiplexer_63 (.in0(multiplexer_31_out), .in1(multiplexer_29_out), .out(multiplexer_63_out), .sel(B[1]));
  Multiplexer multiplexer_64 (.in0(multiplexer_32_out), .in1(multiplexer_30_out), .out(multiplexer_64_out), .sel(B[1]));
  Multiplexer multiplexer_65 (.in0(multiplexer_33_out), .in1(1'b0), .out(multiplexer_65_out), .sel(B[2]));
  Multiplexer multiplexer_66 (.in0(multiplexer_34_out), .in1(1'b0), .out(multiplexer_66_out), .sel(B[2]));
  Multiplexer multiplexer_67 (.in0(multiplexer_35_out), .in1(1'b0), .out(multiplexer_67_out), .sel(B[2]));
  Multiplexer multiplexer_68 (.in0(multiplexer_36_out), .in1(1'b0), .out(multiplexer_68_out), .sel(B[2]));
  Multiplexer multiplexer_69 (.in0(multiplexer_37_out), .in1(multiplexer_33_out), .out(multiplexer_69_out), .sel(B[2]));
  Multiplexer multiplexer_70 (.in0(multiplexer_38_out), .in1(multiplexer_34_out), .out(multiplexer_70_out), .sel(B[2]));
  Multiplexer multiplexer_71 (.in0(multiplexer_39_out), .in1(multiplexer_35_out), .out(multiplexer_71_out), .sel(B[2]));
  Multiplexer multiplexer_72 (.in0(multiplexer_40_out), .in1(multiplexer_36_out), .out(multiplexer_72_out), .sel(B[2]));
  Multiplexer multiplexer_73 (.in0(multiplexer_41_out), .in1(multiplexer_37_out), .out(multiplexer_73_out), .sel(B[2]));
  Multiplexer multiplexer_74 (.in0(multiplexer_42_out), .in1(multiplexer_38_out), .out(multiplexer_74_out), .sel(B[2]));
  Multiplexer multiplexer_75 (.in0(multiplexer_43_out), .in1(multiplexer_39_out), .out(multiplexer_75_out), .sel(B[2]));
  Multiplexer multiplexer_76 (.in0(multiplexer_44_out), .in1(multiplexer_40_out), .out(multiplexer_76_out), .sel(B[2]));
  Multiplexer multiplexer_77 (.in0(multiplexer_45_out), .in1(multiplexer_41_out), .out(multiplexer_77_out), .sel(B[2]));
  Multiplexer multiplexer_78 (.in0(multiplexer_46_out), .in1(multiplexer_42_out), .out(multiplexer_78_out), .sel(B[2]));
  Multiplexer multiplexer_79 (.in0(multiplexer_47_out), .in1(multiplexer_43_out), .out(multiplexer_79_out), .sel(B[2]));
  Multiplexer multiplexer_80 (.in0(multiplexer_48_out), .in1(multiplexer_44_out), .out(multiplexer_80_out), .sel(B[2]));
  Multiplexer multiplexer_81 (.in0(multiplexer_49_out), .in1(multiplexer_45_out), .out(multiplexer_81_out), .sel(B[2]));
  Multiplexer multiplexer_82 (.in0(multiplexer_50_out), .in1(multiplexer_46_out), .out(multiplexer_82_out), .sel(B[2]));
  Multiplexer multiplexer_83 (.in0(multiplexer_51_out), .in1(multiplexer_47_out), .out(multiplexer_83_out), .sel(B[2]));
  Multiplexer multiplexer_84 (.in0(multiplexer_52_out), .in1(multiplexer_48_out), .out(multiplexer_84_out), .sel(B[2]));
  Multiplexer multiplexer_85 (.in0(multiplexer_53_out), .in1(multiplexer_49_out), .out(multiplexer_85_out), .sel(B[2]));
  Multiplexer multiplexer_86 (.in0(multiplexer_54_out), .in1(multiplexer_50_out), .out(multiplexer_86_out), .sel(B[2]));
  Multiplexer multiplexer_87 (.in0(multiplexer_55_out), .in1(multiplexer_51_out), .out(multiplexer_87_out), .sel(B[2]));
  Multiplexer multiplexer_88 (.in0(multiplexer_56_out), .in1(multiplexer_52_out), .out(multiplexer_88_out), .sel(B[2]));
  Multiplexer multiplexer_89 (.in0(multiplexer_57_out), .in1(multiplexer_53_out), .out(multiplexer_89_out), .sel(B[2]));
  Multiplexer multiplexer_90 (.in0(multiplexer_58_out), .in1(multiplexer_54_out), .out(multiplexer_90_out), .sel(B[2]));
  Multiplexer multiplexer_91 (.in0(multiplexer_59_out), .in1(multiplexer_55_out), .out(multiplexer_91_out), .sel(B[2]));
  Multiplexer multiplexer_92 (.in0(multiplexer_60_out), .in1(multiplexer_56_out), .out(multiplexer_92_out), .sel(B[2]));
  Multiplexer multiplexer_93 (.in0(multiplexer_61_out), .in1(multiplexer_57_out), .out(multiplexer_93_out), .sel(B[2]));
  Multiplexer multiplexer_94 (.in0(multiplexer_62_out), .in1(multiplexer_58_out), .out(multiplexer_94_out), .sel(B[2]));
  Multiplexer multiplexer_95 (.in0(multiplexer_63_out), .in1(multiplexer_59_out), .out(multiplexer_95_out), .sel(B[2]));
  Multiplexer multiplexer_96 (.in0(multiplexer_64_out), .in1(multiplexer_60_out), .out(multiplexer_96_out), .sel(B[2]));
  Multiplexer multiplexer_97 (.in0(multiplexer_65_out), .in1(1'b0), .out(multiplexer_97_out), .sel(B[3]));
  Multiplexer multiplexer_98 (.in0(multiplexer_66_out), .in1(1'b0), .out(multiplexer_98_out), .sel(B[3]));
  Multiplexer multiplexer_99 (.in0(multiplexer_67_out), .in1(1'b0), .out(multiplexer_99_out), .sel(B[3]));
  Multiplexer multiplexer_100 (.in0(multiplexer_68_out), .in1(1'b0), .out(multiplexer_100_out), .sel(B[3]));
  Multiplexer multiplexer_101 (.in0(multiplexer_69_out), .in1(1'b0), .out(multiplexer_101_out), .sel(B[3]));
  Multiplexer multiplexer_102 (.in0(multiplexer_70_out), .in1(1'b0), .out(multiplexer_102_out), .sel(B[3]));
  Multiplexer multiplexer_103 (.in0(multiplexer_71_out), .in1(1'b0), .out(multiplexer_103_out), .sel(B[3]));
  Multiplexer multiplexer_104 (.in0(multiplexer_72_out), .in1(1'b0), .out(multiplexer_104_out), .sel(B[3]));
  Multiplexer multiplexer_105 (
    .in0(multiplexer_73_out), .in1(multiplexer_65_out), .out(multiplexer_105_out), .sel(B[3]));
  Multiplexer multiplexer_106 (
    .in0(multiplexer_74_out), .in1(multiplexer_66_out), .out(multiplexer_106_out), .sel(B[3]));
  Multiplexer multiplexer_107 (
    .in0(multiplexer_75_out), .in1(multiplexer_67_out), .out(multiplexer_107_out), .sel(B[3]));
  Multiplexer multiplexer_108 (
    .in0(multiplexer_76_out), .in1(multiplexer_68_out), .out(multiplexer_108_out), .sel(B[3]));
  Multiplexer multiplexer_109 (
    .in0(multiplexer_77_out), .in1(multiplexer_69_out), .out(multiplexer_109_out), .sel(B[3]));
  Multiplexer multiplexer_110 (
    .in0(multiplexer_78_out), .in1(multiplexer_70_out), .out(multiplexer_110_out), .sel(B[3]));
  Multiplexer multiplexer_111 (
    .in0(multiplexer_79_out), .in1(multiplexer_71_out), .out(multiplexer_111_out), .sel(B[3]));
  Multiplexer multiplexer_112 (
    .in0(multiplexer_80_out), .in1(multiplexer_72_out), .out(multiplexer_112_out), .sel(B[3]));
  Multiplexer multiplexer_113 (
    .in0(multiplexer_81_out), .in1(multiplexer_73_out), .out(multiplexer_113_out), .sel(B[3]));
  Multiplexer multiplexer_114 (
    .in0(multiplexer_82_out), .in1(multiplexer_74_out), .out(multiplexer_114_out), .sel(B[3]));
  Multiplexer multiplexer_115 (
    .in0(multiplexer_83_out), .in1(multiplexer_75_out), .out(multiplexer_115_out), .sel(B[3]));
  Multiplexer multiplexer_116 (
    .in0(multiplexer_84_out), .in1(multiplexer_76_out), .out(multiplexer_116_out), .sel(B[3]));
  Multiplexer multiplexer_117 (
    .in0(multiplexer_85_out), .in1(multiplexer_77_out), .out(multiplexer_117_out), .sel(B[3]));
  Multiplexer multiplexer_118 (
    .in0(multiplexer_86_out), .in1(multiplexer_78_out), .out(multiplexer_118_out), .sel(B[3]));
  Multiplexer multiplexer_119 (
    .in0(multiplexer_87_out), .in1(multiplexer_79_out), .out(multiplexer_119_out), .sel(B[3]));
  Multiplexer multiplexer_120 (
    .in0(multiplexer_88_out), .in1(multiplexer_80_out), .out(multiplexer_120_out), .sel(B[3]));
  Multiplexer multiplexer_121 (
    .in0(multiplexer_89_out), .in1(multiplexer_81_out), .out(multiplexer_121_out), .sel(B[3]));
  Multiplexer multiplexer_122 (
    .in0(multiplexer_90_out), .in1(multiplexer_82_out), .out(multiplexer_122_out), .sel(B[3]));
  Multiplexer multiplexer_123 (
    .in0(multiplexer_91_out), .in1(multiplexer_83_out), .out(multiplexer_123_out), .sel(B[3]));
  Multiplexer multiplexer_124 (
    .in0(multiplexer_92_out), .in1(multiplexer_84_out), .out(multiplexer_124_out), .sel(B[3]));
  Multiplexer multiplexer_125 (
    .in0(multiplexer_93_out), .in1(multiplexer_85_out), .out(multiplexer_125_out), .sel(B[3]));
  Multiplexer multiplexer_126 (
    .in0(multiplexer_94_out), .in1(multiplexer_86_out), .out(multiplexer_126_out), .sel(B[3]));
  Multiplexer multiplexer_127 (
    .in0(multiplexer_95_out), .in1(multiplexer_87_out), .out(multiplexer_127_out), .sel(B[3]));
  Multiplexer multiplexer_128 (
    .in0(multiplexer_96_out), .in1(multiplexer_88_out), .out(multiplexer_128_out), .sel(B[3]));
  Multiplexer multiplexer_129 (.in0(multiplexer_97_out), .in1(1'b0), .out(multiplexer_129_out), .sel(B[4]));
  Multiplexer multiplexer_130 (.in0(multiplexer_98_out), .in1(1'b0), .out(multiplexer_130_out), .sel(B[4]));
  Multiplexer multiplexer_131 (.in0(multiplexer_99_out), .in1(1'b0), .out(multiplexer_131_out), .sel(B[4]));
  Multiplexer multiplexer_132 (.in0(multiplexer_100_out), .in1(1'b0), .out(multiplexer_132_out), .sel(B[4]));
  Multiplexer multiplexer_133 (.in0(multiplexer_101_out), .in1(1'b0), .out(multiplexer_133_out), .sel(B[4]));
  Multiplexer multiplexer_134 (.in0(multiplexer_102_out), .in1(1'b0), .out(multiplexer_134_out), .sel(B[4]));
  Multiplexer multiplexer_135 (.in0(multiplexer_103_out), .in1(1'b0), .out(multiplexer_135_out), .sel(B[4]));
  Multiplexer multiplexer_136 (.in0(multiplexer_104_out), .in1(1'b0), .out(multiplexer_136_out), .sel(B[4]));
  Multiplexer multiplexer_137 (.in0(multiplexer_105_out), .in1(1'b0), .out(multiplexer_137_out), .sel(B[4]));
  Multiplexer multiplexer_138 (.in0(multiplexer_106_out), .in1(1'b0), .out(multiplexer_138_out), .sel(B[4]));
  Multiplexer multiplexer_139 (.in0(multiplexer_107_out), .in1(1'b0), .out(multiplexer_139_out), .sel(B[4]));
  Multiplexer multiplexer_140 (.in0(multiplexer_108_out), .in1(1'b0), .out(multiplexer_140_out), .sel(B[4]));
  Multiplexer multiplexer_141 (.in0(multiplexer_109_out), .in1(1'b0), .out(multiplexer_141_out), .sel(B[4]));
  Multiplexer multiplexer_142 (.in0(multiplexer_110_out), .in1(1'b0), .out(multiplexer_142_out), .sel(B[4]));
  Multiplexer multiplexer_143 (.in0(multiplexer_111_out), .in1(1'b0), .out(multiplexer_143_out), .sel(B[4]));
  Multiplexer multiplexer_144 (.in0(multiplexer_112_out), .in1(1'b0), .out(multiplexer_144_out), .sel(B[4]));
  Multiplexer multiplexer_145 (
    .in0(multiplexer_113_out), .in1(multiplexer_97_out), .out(multiplexer_145_out), .sel(B[4]));
  Multiplexer multiplexer_146 (
    .in0(multiplexer_114_out), .in1(multiplexer_98_out), .out(multiplexer_146_out), .sel(B[4]));
  Multiplexer multiplexer_147 (
    .in0(multiplexer_115_out), .in1(multiplexer_99_out), .out(multiplexer_147_out), .sel(B[4]));
  Multiplexer multiplexer_148 (
    .in0(multiplexer_116_out), .in1(multiplexer_100_out), .out(multiplexer_148_out), .sel(B[4]));
  Multiplexer multiplexer_149 (
    .in0(multiplexer_117_out), .in1(multiplexer_101_out), .out(multiplexer_149_out), .sel(B[4]));
  Multiplexer multiplexer_150 (
    .in0(multiplexer_118_out), .in1(multiplexer_102_out), .out(multiplexer_150_out), .sel(B[4]));
  Multiplexer multiplexer_151 (
    .in0(multiplexer_119_out), .in1(multiplexer_103_out), .out(multiplexer_151_out), .sel(B[4]));
  Multiplexer multiplexer_152 (
    .in0(multiplexer_120_out), .in1(multiplexer_104_out), .out(multiplexer_152_out), .sel(B[4]));
  Multiplexer multiplexer_153 (
    .in0(multiplexer_121_out), .in1(multiplexer_105_out), .out(multiplexer_153_out), .sel(B[4]));
  Multiplexer multiplexer_154 (
    .in0(multiplexer_122_out), .in1(multiplexer_106_out), .out(multiplexer_154_out), .sel(B[4]));
  Multiplexer multiplexer_155 (
    .in0(multiplexer_123_out), .in1(multiplexer_107_out), .out(multiplexer_155_out), .sel(B[4]));
  Multiplexer multiplexer_156 (
    .in0(multiplexer_124_out), .in1(multiplexer_108_out), .out(multiplexer_156_out), .sel(B[4]));
  Multiplexer multiplexer_157 (
    .in0(multiplexer_125_out), .in1(multiplexer_109_out), .out(multiplexer_157_out), .sel(B[4]));
  Multiplexer multiplexer_158 (
    .in0(multiplexer_126_out), .in1(multiplexer_110_out), .out(multiplexer_158_out), .sel(B[4]));
  Multiplexer multiplexer_159 (
    .in0(multiplexer_127_out), .in1(multiplexer_111_out), .out(multiplexer_159_out), .sel(B[4]));
  Multiplexer multiplexer_160 (
    .in0(multiplexer_128_out), .in1(multiplexer_112_out), .out(multiplexer_160_out), .sel(B[4]));
  Multiplexer multiplexer_161 (.in0(multiplexer_129_out), .in1(1'b0), .out(sDesl[0]), .sel(or_1_out));
  Multiplexer multiplexer_162 (.in0(multiplexer_130_out), .in1(1'b0), .out(sDesl[1]), .sel(or_1_out));
  Multiplexer multiplexer_163 (.in0(multiplexer_131_out), .in1(1'b0), .out(sDesl[2]), .sel(or_1_out));
  Multiplexer multiplexer_164 (.in0(multiplexer_132_out), .in1(1'b0), .out(sDesl[3]), .sel(or_1_out));
  Multiplexer multiplexer_165 (.in0(multiplexer_133_out), .in1(1'b0), .out(sDesl[4]), .sel(or_1_out));
  Multiplexer multiplexer_166 (.in0(multiplexer_134_out), .in1(1'b0), .out(sDesl[5]), .sel(or_1_out));
  Multiplexer multiplexer_167 (.in0(multiplexer_135_out), .in1(1'b0), .out(sDesl[6]), .sel(or_1_out));
  Multiplexer multiplexer_168 (.in0(multiplexer_136_out), .in1(1'b0), .out(sDesl[7]), .sel(or_1_out));
  Multiplexer multiplexer_169 (.in0(multiplexer_137_out), .in1(1'b0), .out(sDesl[8]), .sel(or_1_out));
  Multiplexer multiplexer_170 (.in0(multiplexer_138_out), .in1(1'b0), .out(sDesl[9]), .sel(or_1_out));
  Multiplexer multiplexer_171 (.in0(multiplexer_139_out), .in1(1'b0), .out(sDesl[10]), .sel(or_1_out));
  Multiplexer multiplexer_172 (.in0(multiplexer_140_out), .in1(1'b0), .out(sDesl[11]), .sel(or_1_out));
  Multiplexer multiplexer_173 (.in0(multiplexer_141_out), .in1(1'b0), .out(sDesl[12]), .sel(or_1_out));
  Multiplexer multiplexer_174 (.in0(multiplexer_142_out), .in1(1'b0), .out(sDesl[13]), .sel(or_1_out));
  Multiplexer multiplexer_175 (.in0(multiplexer_143_out), .in1(1'b0), .out(sDesl[14]), .sel(or_1_out));
  Multiplexer multiplexer_176 (.in0(multiplexer_144_out), .in1(1'b0), .out(sDesl[15]), .sel(or_1_out));
  Multiplexer multiplexer_177 (.in0(multiplexer_145_out), .in1(1'b0), .out(sDesl[16]), .sel(or_1_out));
  Multiplexer multiplexer_178 (.in0(multiplexer_146_out), .in1(1'b0), .out(sDesl[17]), .sel(or_1_out));
  Multiplexer multiplexer_179 (.in0(multiplexer_147_out), .in1(1'b0), .out(sDesl[18]), .sel(or_1_out));
  Multiplexer multiplexer_180 (.in0(multiplexer_148_out), .in1(1'b0), .out(sDesl[19]), .sel(or_1_out));
  Multiplexer multiplexer_181 (.in0(multiplexer_149_out), .in1(1'b0), .out(sDesl[20]), .sel(or_1_out));
  Multiplexer multiplexer_182 (.in0(multiplexer_150_out), .in1(1'b0), .out(sDesl[21]), .sel(or_1_out));
  Multiplexer multiplexer_183 (.in0(multiplexer_151_out), .in1(1'b0), .out(sDesl[22]), .sel(or_1_out));
  Multiplexer multiplexer_184 (.in0(multiplexer_152_out), .in1(1'b0), .out(sDesl[23]), .sel(or_1_out));
  Multiplexer multiplexer_185 (.in0(multiplexer_153_out), .in1(1'b0), .out(sDesl[24]), .sel(or_1_out));
  Multiplexer multiplexer_186 (.in0(multiplexer_154_out), .in1(1'b0), .out(sDesl[25]), .sel(or_1_out));
  Multiplexer multiplexer_187 (.in0(multiplexer_155_out), .in1(1'b0), .out(sDesl[26]), .sel(or_1_out));
  Multiplexer multiplexer_188 (.in0(multiplexer_156_out), .in1(1'b0), .out(sDesl[27]), .sel(or_1_out));
  Multiplexer multiplexer_189 (.in0(multiplexer_157_out), .in1(1'b0), .out(sDesl[28]), .sel(or_1_out));
  Multiplexer multiplexer_190 (.in0(multiplexer_158_out), .in1(1'b0), .out(sDesl[29]), .sel(or_1_out));
  Multiplexer multiplexer_191 (.in0(multiplexer_159_out), .in1(1'b0), .out(sDesl[30]), .sel(or_1_out));
  Multiplexer multiplexer_192 (.in0(multiplexer_160_out), .in1(1'b0), .out(sDesl[31]), .sel(or_1_out));
  or or_1 (or_1_out, B[31], B[30], B[29], B[28], B[27], B[26], B[25], B[24], B[23], B[22], B[21], B[20], B[19], B[18], B[17], B[16], B[15], B[14], B[13], B[12], B[11], B[10], B[9], B[8], B[7], B[6], B[5]);

  // Other names for the same wires on the sheet: s0 = sDesl[0]; s1 = sDesl[1]; s2 = sDesl[2]; s3 = sDesl[3];
  //   s4 = sDesl[4]; s5 = sDesl[5]; s6 = sDesl[6]; s7 = sDesl[7]; s8 = sDesl[8]; s9 = sDesl[9]; s10 = sDesl[10];
  //   s11 = sDesl[11]; s12 = sDesl[12]; s13 = sDesl[13]; s14 = sDesl[14]; s15 = sDesl[15]; s16 = sDesl[16];
  //   s17 = sDesl[17]; s18 = sDesl[18]; s19 = sDesl[19]; s20 = sDesl[20]; s21 = sDesl[21]; s22 = sDesl[22];
  //   s23 = sDesl[23]; s24 = sDesl[24]; s25 = sDesl[25]; s26 = sDesl[26]; s27 = sDesl[27]; s28 = sDesl[28];
  //   s29 = sDesl[29]; s30 = sDesl[30]; s31 = sDesl[31]
endmodule

module extSinal32bits (
  input  [7:0] imm8,
  output [31:0] imm32
);


  assign imm32 = {{25{imm8[7]}}, imm8[6:0]};
endmodule
